// Logisim project CPU_v2.circ as structural Verilog: 11 circuits, main circuit main
module main (
);

  wire clock_1_out, clock_3_out, clock_4_out, clock_5_out, clock_6_out, clock_7_out, dipswitch_1_sw8,
       en_write, op2_is_imm, por_1_out, R, ram_in, ram_ope, small_rd, writeback_alu;
  wire [0:0] clock_2_out;
  wire [1:0] dipswitch_1_sw2, ldiCode, multiplexer_1_out, PcMode;
  wire [3:0] WA_RA1;
  wire [4:0] AluOp;
  wire [5:0] register_1_q;
  wire [7:0] ALU_Result, Immediate, R0, R1, R2, R3, R4, R5, R6, Ram_Data, RD1, RD2, RD2_out, RD3,
       RegFileInput;
  wire [15:0] PcReg;

  POR por_1 (.out(por_1_out));
  Clock clock_1 (.out(clock_1_out));
  // Probe on R0
  // Probe on R1
  // Probe on R2
  // Probe on R3
  // Probe on R4
  // Probe on R5
  // Probe on R6
  // Probe on {R1, R0}
  // Probe on {R3, R2}
  // Probe on {R5, R4}
  // Probe on {R2, R1, R0}
  // Probe on {R5, R4, R3}
  D_Flip_Flop d_ff_1 (.D(por_1_out), .clk(clock_1_out), .Q(R), .preset(por_1_out));  // open: Qn, reset
  // Probe on nothing
  // Probe on R0
  // Probe on R1
  // Probe on R2
  // Probe on R3
  // Probe on R4
  // Probe on R5
  // Probe on R6
  // Probe on {R1, R0}
  // Probe on {R3, R2}
  // Probe on {R5, R4}
  // Probe on {R2, R1, R0}
  // Probe on {R5, R4, R3}
  Clock clock_2 (.out(clock_2_out[0]));
  DipSwitch dipswitch_1 (
    .sw1(dipswitch_1_sw2[1]), .sw2(dipswitch_1_sw2[0]), .sw8(dipswitch_1_sw8));  // open: sw3, sw4, sw5, sw6, sw7
  ROM #(.addrWidth(16)) rom_1 (.addr({PcReg[15:1], clock_2_out[0]}), .data(Immediate));
  RAM #(.addrWidth(16), .enables("line")) ram_1 (
    .addr({RD3, RD2}), .we(ram_in), .clk(clock_3_out), .din(RD1), .dout(Ram_Data));
  Clock clock_3 (.out(clock_3_out));
  Multiplexer #(.width(2)) multiplexer_1 (
    .in0(PcMode), .in1(dipswitch_1_sw2), .out(multiplexer_1_out), .sel(dipswitch_1_sw8));
  Clock clock_4 (.out(clock_4_out));
  RdOut rdout_1 (
    .Imm(Immediate[3:0]), .RamData(Ram_Data[3:0]), .Rd(RD2[3:0]), .RamOpe(ram_ope), .Op2IsImm(op2_is_imm),
    .RdOut(RD2_out[3:0]));
  RdOut rdout_2 (
    .Imm(Immediate[7:4]), .RamData(Ram_Data[7:4]), .Rd(RD2[7:4]), .RamOpe(ram_ope), .Op2IsImm(op2_is_imm),
    .RdOut(RD2_out[7:4]));
  Clock clock_5 (.out(clock_5_out));
  Clock clock_6 (.out(clock_6_out));
  LedBar ledbar_1 (
    .led0(RegFileInput[7]), .led1(RegFileInput[6]), .led2(RegFileInput[5]), .led3(RegFileInput[4]),
    .led4(RegFileInput[3]), .led5(RegFileInput[2]), .led6(RegFileInput[1]), .led7(RegFileInput[0]));
  Multiplexer #(.width(8)) multiplexer_2 (.in0(RD2_out), .in1(ALU_Result), .out(RegFileInput), .sel(writeback_alu));
  RegisterFile registerfile_1 (
    .EnableWrite(en_write), .Write(WA_RA1[2:0]), .WriteData(RegFileInput), .PortA(WA_RA1[2:0]),
    .PortB(Immediate[4:2]), .clk(clock_5_out), .R(R), .RD1(RD1), .RD2(RD2), .RD3(RD3), .R6_out(R6),
    .R5_out(R5), .R4_out(R4), .R3_out(R3), .R2_out(R2), .R1_out(R1), .R0_out(R0));
  ALU alu_1 (
    .AluOp(AluOp), .Enable(writeback_alu), .RD1(RD1), .RD2(RD2), .clk(clock_6_out), .R(R), .Result(ALU_Result));
  Register #(.trigger("high")) register_1 (
    .D(Immediate), .clk(clock_7_out), .Q({WA_RA1[1:0], register_1_q}));  // open: en, clr
  Clock clock_7 (.out(clock_7_out));
  ProgramCounter programcounter_1 (
    .RelativeAddr(RD2_out), .AbisoluteAddr({RD3, RD2}), .CounterMode(multiplexer_1_out), .clk(clock_4_out),
    .Reset(R), .PC(PcReg));
  Multiplexer #(.width(2)) multiplexer_3 (.in0(Immediate[1:0]), .in1(ldiCode), .out(WA_RA1[3:2]), .sel(small_rd));
  LedBar ledbar_2 (
    .led0(RD1[7]), .led1(RD1[6]), .led2(RD1[5]), .led3(RD1[4]), .led4(RD1[3]), .led5(RD1[2]), .led6(RD1[1]),
    .led7(RD1[0]));
  LedBar ledbar_3 (
    .led0(RD2_out[7]), .led1(RD2_out[6]), .led2(RD2_out[5]), .led3(RD2_out[4]), .led4(RD2_out[3]),
    .led5(RD2_out[2]), .led6(RD2_out[1]), .led7(RD2_out[0]));
  InstructionDecoder instructiondecoder_1 (
    .opcode(register_1_q), .CounterMode(PcMode), .writebackAlu(writeback_alu), .op2IsImm(op2_is_imm),
    .enWriteReg1(en_write), .smallRd(small_rd), .LdiCode(ldiCode), .RamOut(ram_ope), .RamIn(ram_in));
  InstructionDecoder2 instructiondecoder2_1 (.opcode(register_1_q), .AluOp(AluOp));  // open: pcVal
  LedBar ledbar_4 (
    .led0(RD3[7]), .led1(RD3[6]), .led2(RD3[5]), .led3(RD3[4]), .led4(RD3[3]), .led5(RD3[2]), .led6(RD3[1]),
    .led7(RD3[0]));

  // Other names for the same wires on the sheet: RA2[3:0] = Immediate[5:2]; RD32[15:0] = {RD3, RD2}

  // Notes on the sheet:
  //   contents of rom_1 (hex, n*v repeats v):
  //   0 41 5 2 5 82 5 c2 55 41 55 81 8 48 1 c1 4 55 10 e4 d c6 1 c1 d 86 aa 41 5 42 aa 81 14 42 8 48 1 c1
  //   4 55 10 e4 d c6 1 c1 d 86 7e 41 4 82 4 88 8 42 1 c1 4 55 10 e4 d c6 1 c1 d 86 a 41 14 81 8 46 1e 81
  //   8 48 1 c1 4 55 10 e4 d c6 1 c1 d 86 32 41 14 81 8 48 1e 81 8 48 1 c1 4 55 10 e4 d c6 1 c1 d 86 ff 41
  //   1 81 8 46 0 41 0 81 8 47 1 81 8 48 1 c1 4 55 10 e4 d c6 1 c1 d 86 0 41 1 81 8 48 a 41 5 81 8 49 4 81
  //   8 48 1 c1 4 55 10 e4 d c6 1 c1 d 86 aa 41 0 4a 55 81 8 48 1 c1 4 55 10 e4 d c6 1 c1 d 86 1 41 0 4b
  //   ff 81 8 48 1 c1 4 55 10 e4 d c6 1 c1 d 86 1 41 0 4c 2 81 8 48 1 c1 4 55 10 e4 d c6 1 c1 d 86 4 41 0
  //   4e 2 81 8 48 1 c1 4 55 10 e4 d c6 1 c1 d 86 80 41 0 50 c0 81 8 48 1 c1 4 55 10 e4 d c6 1 c1 d 86 ff
  //   41 1 81 8 46 1 41 0 4d 3 81 8 48 1 c1 4 55 10 e4 d c6 1 c1 d 86 ff 41 1 81 8 46 2 41 0 4f 81 81 8 48
  //   1 c1 4 55 10 e4 d c6 1 c1 d 86 ff 41 f 81 8 51 8 48 1 c1 4 55 10 e4 d c6 1 c1 d 86 f0 41 f 81 8 52
  //   ff 81 8 48 1 c1 4 55 10 e4 d c6 1 c1 d 86 ff 41 55 81 8 53 aa 81 8 48 1 c1 4 55 10 e4 d c6 1 c1 d 86
  //   5 41 5 81 8 54 1 41 10 64 1 c1 4 55 10 e4 d c6 1 c1 d 86 5 41 3 81 8 54 1 41 10 65 1 c1 4 55 10 e4 d
  //   c6 1 c1 d 86 f0 41 f 81 8 55 1 41 10 64 1 c1 4 55 10 e4 d c6 1 c1 d 86 ff 41 1 81 8 46 1 41 10 62 1
  //   c1 4 55 10 e4 d c6 1 c1 d 86 1 41 1 81 8 46 1 41 10 63 1 c1 4 55 10 e4 d c6 1 c1 d 86 80 41 0 81 8
  //   46 1 41 10 66 1 c1 4 55 10 e4 d c6 1 c1 d 86 7f 41 0 81 8 46 1 41 10 67 1 c1 4 55 10 e4 d c6 1 c1 d
  //   86 7f 41 1 81 8 46 1 41 10 68 1 c1 4 55 10 e4 d c6 1 c1 d 86 1 41 1 81 8 46 1 41 10 69 1 c1 4 55 10
  //   e4 d c6 1 c1 d 86 0 3 1 41 10 60 1 c1 4 55 10 e4 d c6 1 c1 d 86 0 41 1 81 8 61 1 c1 4 55 10 e4 d c6
  //   1 c1 d 86 a 41 5 81 8 54 1 41 10 62 1 c1 4 55 10 e4 d c6 1 c1 d 86 3 41 a 81 8 54 1 41 10 63 1 c1 4
  //   55 10 e4 d c6 1 c1 d 86 5 41 5 81 8 54 1 41 10 6a 1 c1 4 55 10 e4 d c6 1 c1 d 86 a 41 5 81 8 54 1 41
  //   10 6b 1 c1 4 55 10 e4 d c6 1 c1 d 86 5 41 3 81 8 54 1 41 10 6d 1 c1 4 55 10 e4 d c6 1 c1 d 86 ff 41
  //   1 81 8 54 1 41 10 6c 1 c1 4 55 10 e4 d c6 1 c1 d 86 3 41 3 81 8 54 1 41 10 6e 1 c1 4 55 10 e4 d c6 1
  //   c1 d 86 5 41 3 81 8 54 1 41 10 6f 1 c1 4 55 10 e4 d c6 1 c1 d 86 ff 41 5 42 0 41 4 54 1 56 1 56 1 41
  //   10 64 1 c1 4 55 10 e4 d c6 1 c1 d 86 0 41 4 54 ab 41 0 81 f0 c1 8 5f 0 41 8 5e ab 81 8 48 1 c1 4 55
  //   10 e4 d c6 1 c1 d 86 cd 41 2 81 f0 c1 8 5f 0 41 0 81 f0 c1 8 5e ab 81 8 48 1 c1 4 55 10 e4 d c6 1 c1
  //   d 86 0 5c 0 9d 76 57 3 97 4 c2 14 c8 0 41 c 65 1 c1 4 55 10 e4 d c6 1 c1 d 86 0 41 4 3 1 41 1 c1 4
  //   55 10 e4 d c6 1 c1 d 86 4 41 5 42 0 41 14 4 1 41 1 c1 4 55 10 e4 d c6 1 c1 d 86 0 41 c4 81 3 c1 8 5
  //   1 41 1 c1 4 55 10 e4 d c6 1 c1 d 86 0 41 6*0 1 c1 4 55 10 e4 d c6 1 c1 d 86 0 3
endmodule

module PLA_Decoder_LOp (
  input  [3:0] LOp,
  input  [3:0] RD2,
  input  [3:0] RD1,
  output Swap,
  output [3:0] result
);

  PLA #(.in_width(12), .out_width(1), .\table ("xxxxxxxx1111 1")) pla_1 (.in({RD1, RD2, LOp}), .out(Swap));
  PLA #(.in_width(12), .out_width(1), .\table ("xxx0xxx0xxx1 1\nxxx0xxx1xx1x 1\nxxx1xxx0x1xx 1\nxxx1xxx11xxx 1")) pla_2 (
    .in({RD1, RD2, LOp}), .out(result[0]));
  PLA #(.in_width(12), .out_width(1), .\table ("xx0xxx0xxxx1 1\nxx0xxx1xxx1x 1\nxx1xxx0xx1xx 1\nxx1xxx1x1xxx 1")) pla_3 (
    .in({RD1, RD2, LOp}), .out(result[1]));
  PLA #(.in_width(12), .out_width(1), .\table ("x0xxx0xxxxx1 1\nx0xxx1xxxx1x 1\nx1xxx0xxx1xx 1\nx1xxx1xx1xxx 1")) pla_4 (
    .in({RD1, RD2, LOp}), .out(result[2]));
  PLA #(.in_width(12), .out_width(1), .\table ("0xxx0xxxxxx1 1\n0xxx1xxxxx1x 1\n1xxx0xxxx1xx 1\n1xxx1xxx1xxx 1")) pla_5 (
    .in({RD1, RD2, LOp}), .out(result[3]));
endmodule

module RegisterFile (
  input  EnableWrite,
  input  [2:0] Write,
  input  [7:0] WriteData,
  input  [2:0] PortA,
  input  [2:0] PortB,
  input  clk,
  input  R,
  output [7:0] RD1,
  output [7:0] RD2,
  output [7:0] RD3,
  output [7:0] R6_out,
  output [7:0] R5_out,
  output [7:0] R4_out,
  output [7:0] R3_out,
  output [7:0] R2_out,
  output [7:0] R1_out,
  output [7:0] R0_out
);

  wire decoder_1_out1, decoder_1_out2, decoder_1_out3, decoder_1_out4, decoder_1_out5, decoder_1_out6,
       decoder_1_out7, decoder_2_out0, decoder_2_out1, decoder_2_out2, decoder_2_out3, decoder_2_out4,
       decoder_2_out5, decoder_2_out6, decoder_2_out7, decoder_3_out0, decoder_3_out1, decoder_3_out2,
       decoder_3_out3, decoder_3_out4, decoder_3_out5, decoder_3_out6, decoder_3_out7;

  Decoder #(.select(3)) decoder_1 (
    .out1(decoder_1_out1), .out2(decoder_1_out2), .out3(decoder_1_out3), .out4(decoder_1_out4),
    .out5(decoder_1_out5), .out6(decoder_1_out6), .out7(decoder_1_out7), .sel(Write), .en(EnableWrite));  // open: out0
  LedBar ledbar_1 (
    .led0(WriteData[7]), .led1(WriteData[6]), .led2(WriteData[5]), .led3(WriteData[4]), .led4(WriteData[3]),
    .led5(WriteData[2]), .led6(WriteData[1]), .led7(WriteData[0]));
  Register R6 (.D(WriteData), .en(decoder_1_out7), .clk(clk), .Q(R6_out), .clr(R));
  Register R5 (.D(WriteData), .en(decoder_1_out6), .clk(clk), .Q(R5_out), .clr(R));
  Register R4 (.D(WriteData), .en(decoder_1_out5), .clk(clk), .Q(R4_out), .clr(R));
  Register R3 (.D(WriteData), .en(decoder_1_out4), .clk(clk), .Q(R3_out), .clr(R));
  Register R2 (.D(WriteData), .en(decoder_1_out3), .clk(clk), .Q(R2_out), .clr(R));
  Register R1 (.D(WriteData), .en(decoder_1_out2), .clk(clk), .Q(R1_out), .clr(R));
  Register R0 (.D(WriteData), .en(decoder_1_out1), .clk(clk), .Q(R0_out), .clr(R));
  Decoder #(.enable("false"), .select(3)) decoder_2 (
    .out0(decoder_2_out0), .out1(decoder_2_out1), .out2(decoder_2_out2), .out3(decoder_2_out3),
    .out4(decoder_2_out4), .out5(decoder_2_out5), .out6(decoder_2_out6), .out7(decoder_2_out7), .sel(PortA));
  assign RD1 = decoder_2_out6 ? R5_out : 8'bz;  // Controlled_Buffer controlled_buffer_1
  assign RD1 = decoder_2_out5 ? R4_out : 8'bz;  // Controlled_Buffer controlled_buffer_2
  assign RD1 = decoder_2_out3 ? R2_out : 8'bz;  // Controlled_Buffer controlled_buffer_3
  assign RD1 = decoder_2_out2 ? R1_out : 8'bz;  // Controlled_Buffer controlled_buffer_4
  Decoder #(.enable("false"), .select(3)) decoder_3 (
    .out0(decoder_3_out0), .out1(decoder_3_out1), .out2(decoder_3_out2), .out3(decoder_3_out3),
    .out4(decoder_3_out4), .out5(decoder_3_out5), .out6(decoder_3_out6), .out7(decoder_3_out7), .sel(PortB));
  assign RD1 = decoder_2_out7 ? R6_out : 8'bz;  // Controlled_Buffer controlled_buffer_5
  assign RD1 = decoder_2_out4 ? R3_out : 8'bz;  // Controlled_Buffer controlled_buffer_6
  assign RD1 = decoder_2_out1 ? R0_out : 8'bz;  // Controlled_Buffer controlled_buffer_7
  assign RD1 = decoder_2_out0 ? {8{1'b0}} : 8'bz;  // Controlled_Buffer controlled_buffer_8
  LedBar ledbar_2 (
    .led0(RD1[7]), .led1(RD1[6]), .led2(RD1[5]), .led3(RD1[4]), .led4(RD1[3]), .led5(RD1[2]), .led6(RD1[1]),
    .led7(RD1[0]));
  assign RD2 = decoder_3_out7 ? R6_out : 8'bz;  // Controlled_Buffer controlled_buffer_9
  assign RD2 = decoder_3_out6 ? R5_out : 8'bz;  // Controlled_Buffer controlled_buffer_10
  assign RD2 = decoder_3_out5 ? R4_out : 8'bz;  // Controlled_Buffer controlled_buffer_11
  assign RD2 = decoder_3_out4 ? R3_out : 8'bz;  // Controlled_Buffer controlled_buffer_12
  assign RD2 = decoder_3_out3 ? R2_out : 8'bz;  // Controlled_Buffer controlled_buffer_13
  assign RD2 = decoder_3_out2 ? R1_out : 8'bz;  // Controlled_Buffer controlled_buffer_14
  assign RD2 = decoder_3_out1 ? R0_out : 8'bz;  // Controlled_Buffer controlled_buffer_15
  assign RD2 = decoder_3_out0 ? {8{1'b0}} : 8'bz;  // Controlled_Buffer controlled_buffer_16
  LedBar ledbar_3 (
    .led0(RD2[7]), .led1(RD2[6]), .led2(RD2[5]), .led3(RD2[4]), .led4(RD2[3]), .led5(RD2[2]), .led6(RD2[1]),
    .led7(RD2[0]));
  assign RD3 = decoder_3_out6 ? R6_out : 8'bz;  // Controlled_Buffer controlled_buffer_17
  assign RD3 = decoder_3_out5 ? R5_out : 8'bz;  // Controlled_Buffer controlled_buffer_18
  assign RD3 = decoder_3_out4 ? R4_out : 8'bz;  // Controlled_Buffer controlled_buffer_19
  assign RD3 = decoder_3_out3 ? R3_out : 8'bz;  // Controlled_Buffer controlled_buffer_20
  assign RD3 = decoder_3_out2 ? R2_out : 8'bz;  // Controlled_Buffer controlled_buffer_21
  assign RD3 = decoder_3_out1 ? R1_out : 8'bz;  // Controlled_Buffer controlled_buffer_22
  assign RD3 = decoder_3_out0 ? R0_out : 8'bz;  // Controlled_Buffer controlled_buffer_23
  assign RD3 = decoder_3_out7 ? {8{1'b0}} : 8'bz;  // Controlled_Buffer controlled_buffer_24
  LedBar ledbar_4 (
    .led0(RD3[7]), .led1(RD3[6]), .led2(RD3[5]), .led3(RD3[4]), .led4(RD3[3]), .led5(RD3[2]), .led6(RD3[1]),
    .led7(RD3[0]));

  // Other names for the same wires on the sheet: EnWr = EnableWrite; R0[7:0] = R0_out; R1[7:0] = R1_out;
  //   R2[7:0] = R2_out; R3[7:0] = R3_out; R4[7:0] = R4_out; R5[7:0] = R5_out; R6[7:0] = R6_out
endmodule

module ALU (
  input  [4:0] AluOp,
  input  Enable,
  input  [7:0] RD1,
  input  [7:0] RD2,
  input  clk,
  input  R,
  output [7:0] Result
);

  wire adder_1_cout, ALU_A_Sign, ALU_B_Sign, ALU_Carry, ALU_Carry_IN, ALU_OverFlow, ALU_Zero, and_1_out,
       condMatch_out, Flags_Carry, Flags_OutSign, Flags_Overflow, flags_swap, Flags_Zero, multiplexer_3_out,
       nor_1_out, nor_2_out, xor_1_out, xor_2_out;
  wire [1:0] COp, SOp;
  wire [3:0] LOp, multiplexer_2_out;
  wire [6:0] multiplexer_1_out, pla_decoder_lop_1_result;
  wire [7:0] ALU, bit_extender_1_out;

  LedBar #(.matrixcols(5)) ledbar_1 (
    .led0(AluOp[4]), .led1(AluOp[3]), .led2(AluOp[2]), .led3(AluOp[1]), .led4(AluOp[0]));
  Multiplexer #(.select(2), .width(8)) multiplexer_1 (
    .in0({8{1'b0}}), .in1(RD1), .in2({RD1[6:0], ALU_Carry_IN}), .in3({ALU_Carry_IN, RD1[7:1]}),
    .out({ALU_A_Sign, multiplexer_1_out}), .sel(SOp));
  LedBar #(.matrixcols(2)) ledbar_2 (.led0(COp[1]), .led1(COp[0]));
  ALU_InstructionDecode alu_instructiondecode_1 (
    .F(AluOp), .CondMatch(condMatch_out), .COp(COp), .SOp(SOp), .InvRHS(LOp));
  PLA_Decoder_LOp pla_decoder_lop_1 (
    .LOp(LOp), .RD2(RD2[3:0]), .RD1(RD1[3:0]), .Swap(flags_swap), .result(pla_decoder_lop_1_result[3:0]));
  PLA_Decoder_LOp pla_decoder_lop_2 (
    .LOp(LOp), .RD2(RD2[7:4]), .RD1(RD1[7:4]), .result({ALU_B_Sign, pla_decoder_lop_1_result[6:4]}));  // open: Swap
  Multiplexer #(.width(4)) multiplexer_2 (
    .in0({ALU_OverFlow, ALU[7], ALU_Zero, ALU_Carry}), .in1(RD1[3:0]), .out(multiplexer_2_out),
    .sel(flags_swap));
  Register #(.width(4)) Flags (
    .D(multiplexer_2_out), .en(and_1_out), .clk(clk),
    .Q({Flags_Overflow, Flags_OutSign, Flags_Zero, Flags_Carry}), .clr(R));
  and and_1 (and_1_out, Enable, ~AluOp[4]);  // AND_Gate
  LedBar #(.matrixcols(2)) ledbar_3 (.led0(SOp[1]), .led1(SOp[0]));
  Multiplexer #(.select(2)) multiplexer_3 (
    .in0(ALU_Carry_IN), .in1(ALU_Carry_IN), .in2(1'b0), .in3(1'b0), .out(multiplexer_3_out), .sel(SOp));
  Adder adder_1 (
    .a({ALU_A_Sign, multiplexer_1_out}), .b({ALU_B_Sign, pla_decoder_lop_1_result}), .out(ALU),
    .cin(multiplexer_3_out), .cout(adder_1_cout));
  Multiplexer #(.select(2)) multiplexer_4 (
    .in0(adder_1_cout), .in1(adder_1_cout), .in2(RD1[7]), .in3(RD1[0]), .out(ALU_Carry), .sel(SOp));
  LedBar #(.matrixcols(4)) ledbar_4 (.led0(LOp[3]), .led1(LOp[2]), .led2(LOp[1]), .led3(LOp[0]));
  nor nor_1 (nor_1_out, ALU[0], ALU[1], ALU[2], ALU[3]);
  nor nor_2 (nor_2_out, ALU[4], ALU[5], ALU[6], ALU[7]);
  and and_2 (ALU_Zero, nor_1_out, nor_2_out);
  Multiplexer #(.select(2)) multiplexer_5 (
    .in0(1'b0), .in1(1'b1), .in2(RD1[7]), .in3(Flags_Carry), .out(ALU_Carry_IN), .sel(COp));
  xor xor_1 (xor_1_out, ALU[7], ALU_A_Sign);
  xor xor_2 (xor_2_out, ALU[7], ALU_B_Sign);
  and and_3 (ALU_OverFlow, xor_1_out, xor_2_out);
  condMatch condmatch_1 (
    .flagsCarry(Flags_Carry), .flagsZero(Flags_Zero), .flagsOutSign(Flags_OutSign),
    .flagsOverFlow(Flags_Overflow), .AluOp(AluOp[3:0]), .condMatch(condMatch_out));
  assign bit_extender_1_out = {{4{1'b0}}, {Flags_Overflow, Flags_OutSign, Flags_Zero, Flags_Carry}};  // Bit_Extender bit_extender_1
  Multiplexer #(.width(8)) multiplexer_6 (.in0(ALU), .in1(bit_extender_1_out), .out(Result), .sel(flags_swap));

  // Other names for the same wires on the sheet: ALU_Out_Sign = ALU[7];
  //   FlagsReg[3:0] = {Flags_Overflow, Flags_OutSign, Flags_Zero, Flags_Carry}; writeback_alu = Enable
endmodule

module ProgramCounter (
  input  [7:0] RelativeAddr,
  input  [15:0] AbisoluteAddr,
  input  [1:0] CounterMode,
  input  clk,
  input  Reset,
  output [15:0] PC
);

  wire [15:0] adder_1_out, adder_2_out, bit_extender_1_out, multiplexer_1_out;

  Adder #(.width(16)) adder_1 (.a(PC), .b(16'h2), .out(adder_1_out));  // open: cin, cout
  Adder #(.width(16)) adder_2 (.a(PC), .b(bit_extender_1_out), .out(adder_2_out));  // open: cin, cout
  assign bit_extender_1_out = {{8{RelativeAddr[7]}}, RelativeAddr};  // Bit_Extender bit_extender_1
  Register #(.width(16)) register_1 (.D(multiplexer_1_out), .clk(clk), .Q(PC), .clr(Reset));  // open: en
  Multiplexer #(.select(2), .width(16)) multiplexer_1 (
    .in0(adder_1_out), .in1(adder_2_out), .in2(AbisoluteAddr), .out(multiplexer_1_out), .sel(CounterMode));  // open: in3
endmodule

module ALU_InstructionDecode (
  input  [4:0] F,
  input  CondMatch,
  output [1:0] COp,
  output [1:0] SOp,
  output [3:0] InvRHS
);

  wire and_1_out, and_2_out, and_3_out, and_4_out, and_5_out, and_6_out, and_7_out, and_8_out, and_9_out,
       and_10_out, and_11_out, and_12_out, and_13_out, and_14_out, and_15_out, and_16_out, and_17_out,
       and_18_out, and_19_out, and_20_out, and_21_out, and_22_out, and_23_out, and_24_out, and_25_out,
       and_26_out, and_27_out, and_28_out, and_29_out, and_30_out, and_31_out, and_32_out, and_33_out,
       and_34_out, and_35_out, and_36_out, and_37_out, and_38_out, and_39_out, and_40_out, and_41_out,
       and_42_out, and_43_out, and_44_out, and_45_out, and_46_out, and_47_out, and_48_out, and_49_out,
       and_50_out, CondMatch_n, F0_n, F1_n, F2_n, F3_n, F4_n, L_t0_fb315c2c, L_t1_8538ba9c, L_t2_610255f9,
       L_t3_b93ac80a, L_t4_27e1ffd1, L_t5_661cddb1, L_t6_83fb155d, L_t7_a200fe6e, L_t8_2d9f5691,
       L_t9_b73309d5, L_t10_34155c19, L_t11_cd685d4c, L_t12_03850f99, L_t13_8ae765ca, L_t14_078aaaa5,
       L_t15_4a58b767, L_t16_94f4e8ee, L_t17_1143d86b, L_t18_0e53b527, L_t19_a03961f0, L_t20_e6c46511,
       L_t21_4a39d9f8, L_t22_6b47b183, L_t23_9c08840e, L_t24_9ba6a793, L_t25_b4f2e619, L_t26_7c37bb9b,
       L_t27_dad50eff, L_t28_726431d3, L_t29_e243c80c, or_1_out, or_2_out, or_3_out, or_5_out, or_6_out,
       or_8_out, or_11_out, or_12_out, or_14_out, or_15_out, or_17_out, or_18_out, or_20_out, or_22_out;

  not not_1 (F4_n, F[4]);
  not not_2 (F3_n, F[3]);
  not not_3 (F2_n, F[2]);
  not not_4 (F1_n, F[1]);
  not not_5 (F0_n, F[0]);
  not not_6 (CondMatch_n, CondMatch);
  and and_1 (and_1_out, F4_n, F[3]);
  and and_2 (and_2_out, F2_n, F[1]);
  and and_3 (and_3_out, F4_n, F3_n);
  and and_4 (and_4_out, F[1], F[0]);
  and and_5 (and_5_out, F2_n, F[0]);
  and and_6 (and_6_out, F4_n, F3_n);
  and and_7 (and_7_out, F[2], and_8_out);
  and and_8 (and_8_out, F1_n, F[0]);
  and and_9 (and_9_out, F4_n, F3_n);
  and and_10 (and_10_out, F[1], F[0]);
  and and_11 (and_11_out, F4_n, F3_n);
  and and_12 (and_12_out, F2_n, F[1]);
  and and_13 (and_13_out, F2_n, F[0]);
  and and_14 (and_14_out, F4_n, F3_n);
  and and_15 (and_15_out, F[2], F[1]);
  and and_16 (and_16_out, F[3], F2_n);
  and and_17 (and_17_out, F4_n, F3_n);
  and and_18 (and_18_out, F2_n, F1_n);
  and and_19 (and_19_out, F[3], F2_n);
  and and_20 (and_20_out, F4_n, F3_n);
  and and_21 (and_21_out, F2_n, F[1]);
  and and_22 (and_22_out, F[2], F1_n);
  and and_23 (and_23_out, F4_n, F[3]);
  and and_24 (and_24_out, F[2], F0_n);
  and and_25 (and_25_out, F4_n, F3_n);
  and and_26 (and_26_out, F2_n, F1_n);
  and and_27 (and_27_out, F4_n, F[3]);
  and and_28 (and_28_out, F[1], F[0]);
  and and_29 (and_29_out, F4_n, F[3]);
  and and_30 (and_30_out, F[2], F0_n);
  and and_31 (and_31_out, F4_n, F3_n);
  and and_32 (and_32_out, F2_n, F[1]);
  and and_33 (and_33_out, F4_n, F3_n);
  and and_34 (and_34_out, F[2], and_35_out);
  and and_35 (and_35_out, F1_n, F[0]);
  and and_36 (and_36_out, F4_n, F[2]);
  and and_37 (and_37_out, F1_n, F0_n);
  and and_38 (and_38_out, F4_n, F[3]);
  and and_39 (and_39_out, F[1], F[0]);
  and and_40 (and_40_out, F4_n, F[3]);
  and and_41 (and_41_out, F[2], F0_n);
  and and_42 (and_42_out, F4_n, F3_n);
  and and_43 (and_43_out, F2_n, F1_n);
  and and_44 (and_44_out, F4_n, F3_n);
  and and_45 (and_45_out, F[2], and_46_out);
  and and_46 (and_46_out, F1_n, F[0]);
  and and_47 (and_47_out, F4_n, F[2]);
  and and_48 (and_48_out, F1_n, F0_n);
  and and_49 (and_49_out, F4_n, F3_n);
  and and_50 (and_50_out, F2_n, F[1]);
  and and_51 (L_t0_fb315c2c, and_1_out, and_2_out);
  and and_52 (L_t1_8538ba9c, and_3_out, and_4_out);
  and and_53 (L_t2_610255f9, F4_n, and_5_out);
  and and_54 (L_t3_b93ac80a, and_6_out, and_7_out);
  and and_55 (L_t4_27e1ffd1, and_9_out, and_10_out);
  and and_56 (L_t5_661cddb1, and_11_out, and_12_out);
  and and_57 (L_t6_83fb155d, F4_n, and_13_out);
  and and_58 (L_t7_a200fe6e, and_14_out, and_15_out);
  and and_59 (L_t8_2d9f5691, F4_n, and_16_out);
  and and_60 (L_t9_b73309d5, and_17_out, and_18_out);
  and and_61 (L_t10_34155c19, F4_n, and_19_out);
  and and_62 (L_t11_cd685d4c, and_20_out, and_21_out);
  and and_63 (L_t12_03850f99, F[3], and_22_out);
  and and_64 (L_t13_8ae765ca, and_23_out, and_24_out);
  and and_65 (L_t14_078aaaa5, and_25_out, and_26_out);
  and and_66 (L_t15_4a58b767, F[4], CondMatch_n);
  and and_67 (L_t16_94f4e8ee, F[4], CondMatch);
  and and_68 (L_t17_1143d86b, and_27_out, and_28_out);
  and and_69 (L_t18_0e53b527, and_29_out, and_30_out);
  and and_70 (L_t19_a03961f0, F[4], CondMatch_n);
  and and_71 (L_t20_e6c46511, and_31_out, and_32_out);
  and and_72 (L_t21_4a39d9f8, and_33_out, and_34_out);
  and and_73 (L_t22_6b47b183, and_36_out, and_37_out);
  and and_74 (L_t23_9c08840e, and_38_out, and_39_out);
  and and_75 (L_t24_9ba6a793, and_40_out, and_41_out);
  and and_76 (L_t25_b4f2e619, and_42_out, and_43_out);
  and and_77 (L_t26_7c37bb9b, F[4], CondMatch);
  and and_78 (L_t27_dad50eff, and_44_out, and_45_out);
  and and_79 (L_t28_726431d3, and_47_out, and_48_out);
  and and_80 (L_t29_e243c80c, and_49_out, and_50_out);
  or or_1 (or_1_out, L_t15_4a58b767, L_t16_94f4e8ee);
  or or_2 (or_2_out, L_t22_6b47b183, L_t23_9c08840e);
  or or_3 (or_3_out, L_t25_b4f2e619, L_t26_7c37bb9b);
  or or_4 (COp[1], L_t0_fb315c2c, or_5_out);
  or or_5 (or_5_out, L_t1_8538ba9c, L_t2_610255f9);
  or or_6 (or_6_out, L_t3_b93ac80a, L_t4_27e1ffd1);
  or or_7 (COp[0], or_6_out, or_8_out);
  or or_8 (or_8_out, L_t5_661cddb1, L_t6_83fb155d);
  or or_9 (SOp[1], L_t7_a200fe6e, L_t8_2d9f5691);
  or or_10 (SOp[0], L_t9_b73309d5, or_11_out);
  or or_11 (or_11_out, L_t10_34155c19, L_t11_cd685d4c);
  or or_12 (or_12_out, L_t12_03850f99, L_t13_8ae765ca);
  or or_13 (InvRHS[3], or_12_out, or_14_out);
  or or_14 (or_14_out, L_t14_078aaaa5, or_1_out);
  or or_15 (or_15_out, L_t17_1143d86b, L_t18_0e53b527);
  or or_16 (InvRHS[2], or_15_out, or_17_out);
  or or_17 (or_17_out, L_t19_a03961f0, L_t20_e6c46511);
  or or_18 (or_18_out, L_t21_4a39d9f8, or_2_out);
  or or_19 (InvRHS[1], or_18_out, or_20_out);
  or or_20 (or_20_out, L_t24_9ba6a793, or_3_out);
  or or_21 (InvRHS[0], L_t27_dad50eff, or_22_out);
  or or_22 (or_22_out, L_t28_726431d3, L_t29_e243c80c);

  // Other names for the same wires on the sheet: L_go_COp0_40f31696 = COp[0]; L_go_COp1_d72c5142 = COp[1];
  //   L_go_InvRHS0_3fd1a297 = InvRHS[0]; L_go_InvRHS1_224f5061 = InvRHS[1]; L_go_InvRHS2_074757c1 = InvRHS[2];
  //   L_go_InvRHS3_c0d532dc = InvRHS[3]; L_go_SOp0_f96ba0a6 = SOp[0]; L_go_SOp1_b72989e7 = SOp[1]
endmodule

module ALU_logic (
  input  [3:0] A,
  input  [3:0] B,
  input  [3:0] L,
  output [3:0] Z
);

  wire A0_n, A1_n, A2_n, A3_n, and_1_out, and_2_out, and_3_out, and_4_out, and_5_out, and_6_out, and_7_out,
       and_8_out, and_9_out, and_10_out, and_11_out, and_12_out, and_13_out, and_14_out, and_15_out,
       and_16_out, B0_n, B1_n, B2_n, B3_n, L0_n, L1_n, L2_n, L3_n, L_t0_2ce218a3, L_t1_1db98c8c,
       L_t2_3ebf5bc4, L_t3_742b6508, L_t4_ea63257e, L_t5_d22046c6, L_t6_a4ffab2d, L_t7_e16ba892,
       L_t8_526f6f34, L_t9_83fb02a8, L_t10_697ddb87, L_t11_09899771, L_t12_e02cca18, L_t13_04b0a4c7,
       L_t14_d184d39a, L_t15_54a5c1f0, or_1_out, or_2_out, or_3_out, or_4_out, or_5_out, or_6_out, or_7_out,
       or_8_out;

  not not_1 (A3_n, A[3]);
  not not_2 (A2_n, A[2]);
  not not_3 (A1_n, A[1]);
  not not_4 (A0_n, A[0]);
  not not_5 (B3_n, B[3]);
  not not_6 (B2_n, B[2]);
  not not_7 (B1_n, B[1]);
  not not_8 (B0_n, B[0]);
  not not_9 (L3_n, L[3]);
  not not_10 (L2_n, L[2]);
  not not_11 (L1_n, L[1]);
  not not_12 (L0_n, L[0]);
  and and_1 (and_1_out, B[3], L[3]);
  and and_2 (and_2_out, B3_n, L[2]);
  and and_3 (and_3_out, B[3], L[1]);
  and and_4 (and_4_out, B3_n, L[0]);
  and and_5 (and_5_out, B[2], L[3]);
  and and_6 (and_6_out, B2_n, L[2]);
  and and_7 (and_7_out, B[2], L[1]);
  and and_8 (and_8_out, B2_n, L[0]);
  and and_9 (and_9_out, B[1], L[3]);
  and and_10 (and_10_out, B1_n, L[2]);
  and and_11 (and_11_out, B[1], L[1]);
  and and_12 (and_12_out, B1_n, L[0]);
  and and_13 (and_13_out, B[0], L[3]);
  and and_14 (and_14_out, B0_n, L[2]);
  and and_15 (and_15_out, B[0], L[1]);
  and and_16 (and_16_out, B0_n, L[0]);
  and and_17 (L_t0_2ce218a3, A[3], and_1_out);
  and and_18 (L_t1_1db98c8c, A[3], and_2_out);
  and and_19 (L_t2_3ebf5bc4, A3_n, and_3_out);
  and and_20 (L_t3_742b6508, A3_n, and_4_out);
  and and_21 (L_t4_ea63257e, A[2], and_5_out);
  and and_22 (L_t5_d22046c6, A[2], and_6_out);
  and and_23 (L_t6_a4ffab2d, A2_n, and_7_out);
  and and_24 (L_t7_e16ba892, A2_n, and_8_out);
  and and_25 (L_t8_526f6f34, A[1], and_9_out);
  and and_26 (L_t9_83fb02a8, A[1], and_10_out);
  and and_27 (L_t10_697ddb87, A1_n, and_11_out);
  and and_28 (L_t11_09899771, A1_n, and_12_out);
  and and_29 (L_t12_e02cca18, A[0], and_13_out);
  and and_30 (L_t13_04b0a4c7, A[0], and_14_out);
  and and_31 (L_t14_d184d39a, A0_n, and_15_out);
  and and_32 (L_t15_54a5c1f0, A0_n, and_16_out);
  or or_1 (or_1_out, L_t0_2ce218a3, L_t1_1db98c8c);
  or or_2 (or_2_out, L_t2_3ebf5bc4, L_t3_742b6508);
  or or_3 (or_3_out, L_t4_ea63257e, L_t5_d22046c6);
  or or_4 (or_4_out, L_t6_a4ffab2d, L_t7_e16ba892);
  or or_5 (or_5_out, L_t8_526f6f34, L_t9_83fb02a8);
  or or_6 (or_6_out, L_t10_697ddb87, L_t11_09899771);
  or or_7 (or_7_out, L_t12_e02cca18, L_t13_04b0a4c7);
  or or_8 (or_8_out, L_t14_d184d39a, L_t15_54a5c1f0);
  or or_9 (Z[3], or_1_out, or_2_out);
  or or_10 (Z[2], or_3_out, or_4_out);
  or or_11 (Z[1], or_5_out, or_6_out);
  or or_12 (Z[0], or_7_out, or_8_out);

  // Other names for the same wires on the sheet: L_go_Z0_f884eed5 = Z[0]; L_go_Z1_0b991dc2 = Z[1];
  //   L_go_Z2_a127165e = Z[2]; L_go_Z3_bfbe8670 = Z[3]
endmodule

module InstructionDecoder (
  input  [5:0] opcode,
  output [1:0] CounterMode,
  output writebackAlu,
  output op2IsImm,
  output enWriteReg1,
  output smallRd,
  output [1:0] LdiCode,
  output RamOut,
  output RamIn
);

  wire and_1_out, and_2_out, and_3_out, and_4_out, and_5_out, and_6_out, and_7_out, and_8_out, and_9_out,
       and_10_out, and_11_out, and_12_out, and_13_out, and_14_out, and_15_out, and_16_out, and_17_out,
       and_18_out, and_19_out, and_21_out, and_22_out, and_24_out, and_25_out, and_27_out, and_29_out,
       and_31_out, and_33_out, and_35_out, and_37_out, and_38_out, and_40_out, and_41_out, and_43_out,
       and_44_out, and_46_out, and_48_out, and_50_out, and_51_out, and_53_out, and_55_out, and_57_out,
       and_61_out, and_63_out, and_64_out, and_66_out, and_68_out, and_70_out, and_71_out, and_73_out,
       and_75_out, and_76_out, and_78_out, and_79_out, and_81_out, L_t1_a73fdba7, L_t2_62af8003,
       L_t3_4493a037, L_t4_bc1bb7ec, L_t5_069adc13, L_t6_9df68c36, L_t8_28333dad, L_t9_a6869663,
       L_t10_a8c43ae6, L_t11_279e081e, L_t12_3bb2e122, L_t13_b370c22e, L_t14_f27648d1, L_t15_d2d6f8c9,
       L_t16_2493c280, L_t17_6e08ab35, L_t18_0d6b634a, L_t19_fddbbc2b, L_t21_0d32c0cc, L_t22_026e92f8,
       L_t23_e53514ad, L_t25_68fb8336, L_t26_2c0960de, opcode0_n, opcode1_n, opcode2_n, opcode3_n, opcode4_n,
       opcode5_n, or_1_out, or_2_out, or_3_out, or_4_out, or_5_out, or_6_out, or_7_out, or_8_out, or_9_out,
       or_10_out, or_11_out, or_12_out, or_13_out;

  not not_1 (opcode5_n, opcode[5]);
  not not_2 (opcode4_n, opcode[4]);
  not not_3 (opcode3_n, opcode[3]);
  not not_4 (opcode2_n, opcode[2]);
  not not_5 (opcode1_n, opcode[1]);
  not not_6 (opcode0_n, opcode[0]);
  and and_1 (and_1_out, opcode4_n, opcode3_n);
  and and_2 (and_2_out, opcode1_n, opcode[0]);
  and and_3 (and_3_out, opcode4_n, opcode3_n);
  and and_4 (and_4_out, opcode1_n, opcode0_n);
  and and_5 (and_5_out, opcode4_n, opcode3_n);
  and and_6 (and_6_out, opcode[1], opcode[0]);
  and and_7 (and_7_out, opcode4_n, opcode3_n);
  and and_8 (and_8_out, opcode[1], opcode[0]);
  and and_9 (and_9_out, opcode4_n, opcode3_n);
  and and_10 (and_10_out, opcode1_n, opcode[0]);
  and and_11 (and_11_out, opcode[1], opcode[0]);
  and and_12 (and_12_out, opcode4_n, opcode3_n);
  and and_13 (and_13_out, opcode1_n, opcode[0]);
  and and_14 (and_14_out, opcode[1], opcode[0]);
  and and_15 (and_15_out, opcode4_n, opcode3_n);
  and and_16 (and_16_out, opcode1_n, opcode[0]);
  and and_17 (and_17_out, opcode[1], opcode[0]);
  and and_18 (and_18_out, opcode[1], opcode[0]);
  and and_19 (and_19_out, opcode5_n, and_1_out);
  and and_20 (CounterMode[1], and_19_out, and_21_out);
  and and_21 (and_21_out, opcode[2], and_2_out);
  and and_22 (and_22_out, opcode5_n, and_3_out);
  and and_23 (L_t1_a73fdba7, and_22_out, and_24_out);
  and and_24 (and_24_out, opcode[2], and_4_out);
  and and_25 (and_25_out, opcode5_n, and_5_out);
  and and_26 (L_t2_62af8003, and_25_out, and_27_out);
  and and_27 (and_27_out, opcode2_n, and_6_out);
  and and_28 (L_t3_4493a037, opcode[4], and_29_out);
  and and_29 (and_29_out, opcode3_n, opcode0_n);
  and and_30 (L_t4_bc1bb7ec, opcode4_n, and_31_out);
  and and_31 (and_31_out, opcode[2], opcode[1]);
  and and_32 (L_t5_069adc13, opcode[4], and_33_out);
  and and_33 (and_33_out, opcode3_n, opcode2_n);
  and and_34 (L_t6_9df68c36, opcode4_n, opcode[3]);
  and and_35 (and_35_out, opcode5_n, and_7_out);
  and and_36 (L_t8_28333dad, and_35_out, and_37_out);
  and and_37 (and_37_out, opcode2_n, and_8_out);
  and and_38 (and_38_out, opcode5_n, and_9_out);
  and and_39 (L_t9_a6869663, and_38_out, and_40_out);
  and and_40 (and_40_out, opcode2_n, and_10_out);
  and and_41 (and_41_out, opcode[4], opcode[3]);
  and and_42 (L_t10_a8c43ae6, and_41_out, and_43_out);
  and and_43 (and_43_out, opcode[1], opcode0_n);
  and and_44 (and_44_out, opcode[4], opcode3_n);
  and and_45 (L_t11_279e081e, and_44_out, and_46_out);
  and and_46 (and_46_out, opcode[2], and_11_out);
  and and_47 (L_t12_3bb2e122, opcode[3], opcode1_n);
  and and_48 (and_48_out, opcode5_n, and_12_out);
  and and_49 (L_t13_b370c22e, and_48_out, and_50_out);
  and and_50 (and_50_out, opcode2_n, and_13_out);
  and and_51 (and_51_out, opcode[4], opcode3_n);
  and and_52 (L_t14_f27648d1, and_51_out, and_53_out);
  and and_53 (and_53_out, opcode[2], and_14_out);
  and and_54 (L_t15_d2d6f8c9, opcode4_n, and_55_out);
  and and_55 (and_55_out, opcode[2], opcode[1]);
  and and_56 (L_t16_2493c280, opcode[4], and_57_out);
  and and_57 (and_57_out, opcode3_n, opcode2_n);
  and and_58 (L_t17_6e08ab35, opcode[1], opcode0_n);
  and and_59 (L_t18_0d6b634a, opcode[3], opcode1_n);
  and and_60 (L_t19_fddbbc2b, opcode4_n, opcode[3]);
  and and_61 (and_61_out, opcode5_n, and_15_out);
  and and_62 (L_t21_0d32c0cc, and_61_out, and_63_out);
  and and_63 (and_63_out, opcode2_n, and_16_out);
  and and_64 (and_64_out, opcode[4], opcode3_n);
  and and_65 (L_t22_026e92f8, and_64_out, and_66_out);
  and and_66 (and_66_out, opcode[2], and_17_out);
  and and_67 (L_t23_e53514ad, opcode[4], and_68_out);
  and and_68 (and_68_out, opcode[3], opcode2_n);
  and and_69 (LdiCode[1], opcode[4], and_70_out);
  and and_70 (and_70_out, opcode[3], opcode2_n);
  and and_71 (and_71_out, opcode[4], opcode3_n);
  and and_72 (L_t25_68fb8336, and_71_out, and_73_out);
  and and_73 (and_73_out, opcode[2], and_18_out);
  and and_74 (L_t26_2c0960de, opcode[4], and_75_out);
  and and_75 (and_75_out, opcode2_n, opcode[0]);
  and and_76 (and_76_out, opcode[4], opcode[3]);
  and and_77 (RamOut, and_76_out, and_78_out);
  and and_78 (and_78_out, opcode[1], opcode0_n);
  and and_79 (and_79_out, opcode[4], opcode[3]);
  and and_80 (RamIn, and_79_out, and_81_out);
  and and_81 (and_81_out, opcode[1], opcode[0]);
  or or_1 (or_1_out, L_t6_9df68c36, opcode[5]);
  or or_2 (or_2_out, L_t11_279e081e, L_t12_3bb2e122);
  or or_3 (or_3_out, L_t13_b370c22e, L_t14_f27648d1);
  or or_4 (or_4_out, L_t15_d2d6f8c9, L_t16_2493c280);
  or or_5 (or_5_out, L_t17_6e08ab35, L_t18_0d6b634a);
  or or_6 (or_6_out, L_t19_fddbbc2b, opcode[5]);
  or or_7 (or_7_out, L_t3_4493a037, L_t4_bc1bb7ec);
  or or_8 (or_8_out, L_t5_069adc13, or_1_out);
  or or_9 (or_9_out, L_t8_28333dad, L_t9_a6869663);
  or or_10 (or_10_out, L_t10_a8c43ae6, or_2_out);
  or or_11 (or_11_out, or_3_out, or_4_out);
  or or_12 (or_12_out, or_5_out, or_6_out);
  or or_13 (or_13_out, L_t22_026e92f8, L_t23_e53514ad);
  or or_14 (CounterMode[0], L_t1_a73fdba7, L_t2_62af8003);
  or or_15 (writebackAlu, or_7_out, or_8_out);
  or or_16 (op2IsImm, or_9_out, or_10_out);
  or or_17 (enWriteReg1, or_11_out, or_12_out);
  or or_18 (smallRd, L_t21_0d32c0cc, or_13_out);
  or or_19 (LdiCode[0], L_t25_68fb8336, L_t26_2c0960de);

  // Other names for the same wires on the sheet: L_go_CounterMode0_0fac5d2a = CounterMode[0];
  //   L_go_CounterMode1_2c727776 = CounterMode[1]; L_t0_8666876d = CounterMode[1]; L_t27_09488bf3 = RamOut;
  //   L_t28_836fbe45 = RamIn; L_go_LdiCode0_97ab421a = LdiCode[0]; L_go_LdiCode1_c871f1d3 = LdiCode[1];
  //   L_t24_ccf35d42 = LdiCode[1]; L_t7_79988837 = opcode[5]; L_t20_77f0f043 = opcode[5]
endmodule

module InstructionDecoder2 (
  input  [5:0] opcode,
  output [1:0] pcVal,
  output [4:0] AluOp
);

  wire and_1_out, and_2_out, and_3_out, and_4_out, and_5_out, and_6_out, and_7_out, and_8_out, and_9_out,
       and_10_out, and_11_out, and_12_out, and_13_out, and_14_out, L_t3_571fdce4, L_t4_652b14fe,
       L_t5_8a8cfd76, L_t6_2c3f994b, L_t7_e3feff47, L_t8_6abbb69f, L_t9_6474a718, L_t10_f690403c,
       L_t11_ce27f1c0, L_t12_1cbc3ac6, L_t13_d2e059bf, L_t14_73fb8264, L_t15_5090e23b, L_t16_695cdf90,
       L_t17_a050b667, opcode0_n, opcode1_n, opcode2_n, opcode3_n, opcode4_n, opcode5_n, or_1_out, or_2_out,
       or_4_out, or_5_out, or_7_out, or_8_out, or_10_out;

  not not_1 (opcode5_n, opcode[5]);
  not not_2 (opcode4_n, opcode[4]);
  not not_3 (opcode3_n, opcode[3]);
  not not_4 (opcode2_n, opcode[2]);
  not not_5 (opcode1_n, opcode[1]);
  not not_6 (opcode0_n, opcode[0]);
  and and_1 (and_1_out, opcode[4], opcode[3]);
  and and_2 (and_2_out, opcode[2], and_3_out);
  and and_3 (and_3_out, opcode1_n, opcode[0]);
  and and_4 (and_4_out, opcode[4], opcode[3]);
  and and_5 (and_5_out, opcode[2], and_6_out);
  and and_6 (and_6_out, opcode1_n, opcode0_n);
  and and_7 (and_7_out, opcode[2], opcode[1]);
  and and_8 (and_8_out, opcode[2], opcode1_n);
  and and_9 (and_9_out, opcode2_n, opcode[1]);
  and and_10 (and_10_out, opcode2_n, opcode[0]);
  and and_11 (and_11_out, opcode1_n, opcode0_n);
  and and_12 (and_12_out, opcode2_n, opcode[1]);
  and and_13 (and_13_out, opcode[3], opcode1_n);
  and and_14 (and_14_out, opcode2_n, opcode[0]);
  and and_15 (pcVal[1], and_1_out, and_2_out);
  and and_16 (pcVal[0], and_4_out, and_5_out);
  and and_17 (L_t3_571fdce4, opcode[3], and_7_out);
  and and_18 (L_t4_652b14fe, opcode[4], opcode2_n);
  and and_19 (L_t5_8a8cfd76, opcode[5], opcode[3]);
  and and_20 (L_t6_2c3f994b, opcode[4], opcode[1]);
  and and_21 (L_t7_e3feff47, opcode4_n, and_8_out);
  and and_22 (L_t8_6abbb69f, opcode5_n, and_9_out);
  and and_23 (L_t9_6474a718, opcode[4], and_10_out);
  and and_24 (L_t10_f690403c, opcode[5], opcode[2]);
  and and_25 (L_t11_ce27f1c0, opcode[4], opcode[1]);
  and and_26 (L_t12_1cbc3ac6, opcode5_n, and_11_out);
  and and_27 (L_t13_d2e059bf, opcode3_n, and_12_out);
  and and_28 (L_t14_73fb8264, opcode5_n, and_13_out);
  and and_29 (L_t15_5090e23b, opcode[5], opcode[1]);
  and and_30 (L_t16_695cdf90, opcode[4], and_14_out);
  and and_31 (L_t17_a050b667, opcode4_n, opcode[0]);
  or or_1 (or_1_out, L_t10_f690403c, L_t11_ce27f1c0);
  or or_2 (or_2_out, L_t3_571fdce4, L_t4_652b14fe);
  or or_3 (AluOp[3], or_2_out, or_4_out);
  or or_4 (or_4_out, L_t5_8a8cfd76, L_t6_2c3f994b);
  or or_5 (or_5_out, L_t7_e3feff47, L_t8_6abbb69f);
  or or_6 (AluOp[2], or_5_out, or_7_out);
  or or_7 (or_7_out, L_t9_6474a718, or_1_out);
  or or_8 (or_8_out, L_t12_1cbc3ac6, L_t13_d2e059bf);
  or or_9 (AluOp[1], or_8_out, or_10_out);
  or or_10 (or_10_out, L_t14_73fb8264, L_t15_5090e23b);
  or or_11 (AluOp[0], L_t16_695cdf90, L_t17_a050b667);

  assign AluOp[4] = opcode[5];

  // Other names for the same wires on the sheet: L_go_AluOp0_0b676e28 = AluOp[0]; L_go_AluOp1_294d7107 = AluOp[1];
  //   L_go_AluOp2_d535449a = AluOp[2]; L_go_AluOp3_c738dfff = AluOp[3]; L_go_AluOp4_6c9eb518 = opcode[5];
  //   L_t2_f272ffd1 = opcode[5]; L_go_pcVal0_9b7a3bbf = pcVal[0]; L_t1_2b390be9 = pcVal[0];
  //   L_go_pcVal1_e8e77d47 = pcVal[1]; L_t0_9f0dfd17 = pcVal[1]
endmodule

module condMatch (
  input  flagsCarry,
  input  flagsZero,
  input  flagsOutSign,
  input  flagsOverFlow,
  input  [3:0] AluOp,
  output condMatch
);

  wire AluOp0_n, AluOp1_n, AluOp2_n, AluOp3_n, and_1_out, and_2_out, and_3_out, and_4_out, and_5_out,
       and_6_out, and_7_out, and_8_out, and_9_out, and_10_out, and_11_out, and_12_out, and_13_out,
       and_14_out, and_15_out, and_16_out, and_17_out, and_18_out, and_19_out, and_20_out, and_21_out,
       and_22_out, and_23_out, and_24_out, and_25_out, and_26_out, and_27_out, and_28_out, and_29_out,
       and_30_out, and_31_out, and_32_out, and_33_out, and_34_out, and_35_out, and_36_out, and_37_out,
       and_38_out, and_39_out, and_40_out, and_41_out, and_42_out, and_43_out, and_44_out, and_45_out,
       and_46_out, and_47_out, and_48_out, and_49_out, and_50_out, and_51_out, and_52_out, flagsCarry_n,
       flagsOutSign_n, flagsOverFlow_n, flagsZero_n, L_t0_358b8dbe, L_t1_e19874f1, L_t2_9f67eb77,
       L_t3_11d638d0, L_t4_4bfa1768, L_t5_66b289f7, L_t6_db6cb29e, L_t7_7d2ba93f, L_t8_8433c662,
       L_t9_097678ee, L_t10_f27be657, L_t11_0f6c49f0, L_t12_d6d48ab4, L_t13_ebc0ab00, L_t14_7245567c,
       L_t15_eaeca90a, L_t16_eff40b24, L_t17_c64e1c66, or_1_out, or_2_out, or_3_out, or_4_out, or_5_out,
       or_6_out, or_7_out, or_8_out, or_9_out, or_10_out, or_11_out, or_12_out, or_13_out, or_14_out,
       or_15_out, or_17_out;

  not not_1 (flagsCarry_n, flagsCarry);
  not not_2 (flagsZero_n, flagsZero);
  not not_3 (flagsOutSign_n, flagsOutSign);
  not not_4 (flagsOverFlow_n, flagsOverFlow);
  not not_5 (AluOp3_n, AluOp[3]);
  not not_6 (AluOp2_n, AluOp[2]);
  not not_7 (AluOp1_n, AluOp[1]);
  not not_8 (AluOp0_n, AluOp[0]);
  and and_1 (and_1_out, flagsOverFlow, AluOp[3]);
  and and_2 (and_2_out, AluOp2_n, and_3_out);
  and and_3 (and_3_out, AluOp1_n, AluOp0_n);
  and and_4 (and_4_out, flagsZero, AluOp3_n);
  and and_5 (and_5_out, AluOp[2], and_6_out);
  and and_6 (and_6_out, AluOp1_n, AluOp0_n);
  and and_7 (and_7_out, flagsOutSign, flagsOverFlow_n);
  and and_8 (and_8_out, AluOp[3], and_9_out);
  and and_9 (and_9_out, AluOp[2], AluOp0_n);
  and and_10 (and_10_out, flagsOutSign_n, flagsOverFlow);
  and and_11 (and_11_out, AluOp[3], and_12_out);
  and and_12 (and_12_out, AluOp[2], AluOp0_n);
  and and_13 (and_13_out, flagsCarry, AluOp3_n);
  and and_14 (and_14_out, AluOp2_n, and_15_out);
  and and_15 (and_15_out, AluOp[1], AluOp0_n);
  and and_16 (and_16_out, flagsCarry_n, AluOp[3]);
  and and_17 (and_17_out, AluOp2_n, and_18_out);
  and and_18 (and_18_out, AluOp[1], AluOp0_n);
  and and_19 (and_19_out, flagsZero, AluOp[3]);
  and and_20 (and_20_out, AluOp[1], AluOp0_n);
  and and_21 (and_21_out, flagsOutSign, AluOp3_n);
  and and_22 (and_22_out, AluOp[2], and_23_out);
  and and_23 (and_23_out, AluOp[1], AluOp0_n);
  and and_24 (and_24_out, AluOp3_n, AluOp2_n);
  and and_25 (and_25_out, AluOp1_n, AluOp[0]);
  and and_26 (and_26_out, flagsOverFlow_n, AluOp2_n);
  and and_27 (and_27_out, AluOp1_n, AluOp[0]);
  and and_28 (and_28_out, flagsZero_n, AluOp3_n);
  and and_29 (and_29_out, AluOp1_n, AluOp[0]);
  and and_30 (and_30_out, flagsZero_n, flagsOutSign_n);
  and and_31 (and_31_out, flagsOverFlow_n, and_32_out);
  and and_32 (and_32_out, AluOp[2], AluOp[0]);
  and and_33 (and_33_out, flagsOutSign_n, flagsOverFlow_n);
  and and_34 (and_34_out, AluOp[3], and_35_out);
  and and_35 (and_35_out, AluOp1_n, AluOp[0]);
  and and_36 (and_36_out, flagsOutSign, and_37_out);
  and and_37 (and_37_out, flagsOverFlow, AluOp[3]);
  and and_38 (and_38_out, AluOp[2], and_39_out);
  and and_39 (and_39_out, AluOp1_n, AluOp[0]);
  and and_40 (and_40_out, flagsCarry_n, AluOp3_n);
  and and_41 (and_41_out, AluOp2_n, AluOp[0]);
  and and_42 (and_42_out, flagsCarry, and_43_out);
  and and_43 (and_43_out, flagsZero_n, AluOp[3]);
  and and_44 (and_44_out, AluOp2_n, and_45_out);
  and and_45 (and_45_out, AluOp[1], AluOp[0]);
  and and_46 (and_46_out, flagsOutSign_n, AluOp3_n);
  and and_47 (and_47_out, AluOp[2], and_48_out);
  and and_48 (and_48_out, AluOp[1], AluOp[0]);
  and and_49 (and_49_out, flagsZero_n, and_50_out);
  and and_50 (and_50_out, flagsOutSign, flagsOverFlow);
  and and_51 (and_51_out, AluOp[3], and_52_out);
  and and_52 (and_52_out, AluOp[2], AluOp[0]);
  and and_53 (L_t0_358b8dbe, and_1_out, and_2_out);
  and and_54 (L_t1_e19874f1, and_4_out, and_5_out);
  and and_55 (L_t2_9f67eb77, and_7_out, and_8_out);
  and and_56 (L_t3_11d638d0, and_10_out, and_11_out);
  and and_57 (L_t4_4bfa1768, and_13_out, and_14_out);
  and and_58 (L_t5_66b289f7, and_16_out, and_17_out);
  and and_59 (L_t6_db6cb29e, and_19_out, and_20_out);
  and and_60 (L_t7_7d2ba93f, and_21_out, and_22_out);
  and and_61 (L_t8_8433c662, and_24_out, and_25_out);
  and and_62 (L_t9_097678ee, and_26_out, and_27_out);
  and and_63 (L_t10_f27be657, and_28_out, and_29_out);
  and and_64 (L_t11_0f6c49f0, and_30_out, and_31_out);
  and and_65 (L_t12_d6d48ab4, and_33_out, and_34_out);
  and and_66 (L_t13_ebc0ab00, and_36_out, and_38_out);
  and and_67 (L_t14_7245567c, and_40_out, and_41_out);
  and and_68 (L_t15_eaeca90a, and_42_out, and_44_out);
  and and_69 (L_t16_eff40b24, and_46_out, and_47_out);
  and and_70 (L_t17_c64e1c66, and_49_out, and_51_out);
  or or_1 (or_1_out, L_t7_7d2ba93f, L_t8_8433c662);
  or or_2 (or_2_out, L_t16_eff40b24, L_t17_c64e1c66);
  or or_3 (or_3_out, L_t0_358b8dbe, L_t1_e19874f1);
  or or_4 (or_4_out, L_t2_9f67eb77, L_t3_11d638d0);
  or or_5 (or_5_out, L_t4_4bfa1768, L_t5_66b289f7);
  or or_6 (or_6_out, L_t6_db6cb29e, or_1_out);
  or or_7 (or_7_out, L_t9_097678ee, L_t10_f27be657);
  or or_8 (or_8_out, L_t11_0f6c49f0, L_t12_d6d48ab4);
  or or_9 (or_9_out, L_t13_ebc0ab00, L_t14_7245567c);
  or or_10 (or_10_out, L_t15_eaeca90a, or_2_out);
  or or_11 (or_11_out, or_3_out, or_4_out);
  or or_12 (or_12_out, or_5_out, or_6_out);
  or or_13 (or_13_out, or_7_out, or_8_out);
  or or_14 (or_14_out, or_9_out, or_10_out);
  or or_15 (or_15_out, or_11_out, or_12_out);
  or or_16 (condMatch, or_15_out, or_17_out);
  or or_17 (or_17_out, or_13_out, or_14_out);
endmodule

module RdOut (
  input  [3:0] Imm,
  input  [3:0] RamData,
  input  [3:0] Rd,
  input  RamOpe,
  input  Op2IsImm,
  output [3:0] RdOut
);

  wire and_1_out, and_2_out, and_3_out, and_4_out, and_5_out, and_6_out, and_7_out, and_8_out, Imm0_n,
       Imm1_n, Imm2_n, Imm3_n, L_t0_4d3ff043, L_t1_9f38a878, L_t2_21bcc1a3, L_t3_17f614f9, L_t4_6df30977,
       L_t5_91c81069, L_t6_bc7d17ee, L_t7_81527391, L_t8_ca8a565c, L_t9_bd565594, L_t10_03821077,
       L_t11_05c56e5a, Op2IsImm_n, or_1_out, or_2_out, or_3_out, or_4_out, RamData0_n, RamData1_n,
       RamData2_n, RamData3_n, RamOpe_n, Rd0_n, Rd1_n, Rd2_n, Rd3_n;

  not not_1 (Imm3_n, Imm[3]);
  not not_2 (Imm2_n, Imm[2]);
  not not_3 (Imm1_n, Imm[1]);
  not not_4 (Imm0_n, Imm[0]);
  not not_5 (RamData3_n, RamData[3]);
  not not_6 (RamData2_n, RamData[2]);
  not not_7 (RamData1_n, RamData[1]);
  not not_8 (RamData0_n, RamData[0]);
  not not_9 (Rd3_n, Rd[3]);
  not not_10 (Rd2_n, Rd[2]);
  not not_11 (Rd1_n, Rd[1]);
  not not_12 (Rd0_n, Rd[0]);
  not not_13 (RamOpe_n, RamOpe);
  not not_14 (Op2IsImm_n, Op2IsImm);
  and and_1 (and_1_out, RamOpe_n, Op2IsImm);
  and and_2 (and_2_out, RamOpe, Op2IsImm);
  and and_3 (and_3_out, RamOpe_n, Op2IsImm);
  and and_4 (and_4_out, RamOpe, Op2IsImm);
  and and_5 (and_5_out, RamOpe_n, Op2IsImm);
  and and_6 (and_6_out, RamOpe, Op2IsImm);
  and and_7 (and_7_out, RamOpe_n, Op2IsImm);
  and and_8 (and_8_out, RamOpe, Op2IsImm);
  and and_9 (L_t0_4d3ff043, Imm[3], and_1_out);
  and and_10 (L_t1_9f38a878, RamData[3], and_2_out);
  and and_11 (L_t2_21bcc1a3, Rd[3], Op2IsImm_n);
  and and_12 (L_t3_17f614f9, Imm[2], and_3_out);
  and and_13 (L_t4_6df30977, RamData[2], and_4_out);
  and and_14 (L_t5_91c81069, Rd[2], Op2IsImm_n);
  and and_15 (L_t6_bc7d17ee, Imm[1], and_5_out);
  and and_16 (L_t7_81527391, RamData[1], and_6_out);
  and and_17 (L_t8_ca8a565c, Rd[1], Op2IsImm_n);
  and and_18 (L_t9_bd565594, Imm[0], and_7_out);
  and and_19 (L_t10_03821077, RamData[0], and_8_out);
  and and_20 (L_t11_05c56e5a, Rd[0], Op2IsImm_n);
  or or_1 (or_1_out, L_t1_9f38a878, L_t2_21bcc1a3);
  or or_2 (or_2_out, L_t4_6df30977, L_t5_91c81069);
  or or_3 (or_3_out, L_t7_81527391, L_t8_ca8a565c);
  or or_4 (or_4_out, L_t10_03821077, L_t11_05c56e5a);
  or or_5 (RdOut[3], L_t0_4d3ff043, or_1_out);
  or or_6 (RdOut[2], L_t3_17f614f9, or_2_out);
  or or_7 (RdOut[1], L_t6_bc7d17ee, or_3_out);
  or or_8 (RdOut[0], L_t9_bd565594, or_4_out);

  // Other names for the same wires on the sheet: L_go_RdOut0_a15231a3 = RdOut[0]; L_go_RdOut1_183e7a46 = RdOut[1];
  //   L_go_RdOut2_c67e323d = RdOut[2]; L_go_RdOut3_18272478 = RdOut[3]
endmodule
