// Logisim project CPU.circ as structural Verilog: 4 circuits, main circuit main
module main (
);

  wire Bus_sel, clk, Mem, nand_1_out, nand_2_out, nand_3_out, nand_4_out, nand_5_out, nand_6_out, nor_1_out,
       nor_2_out, nor_3_out, not_1_out, not_2_out, not_3_out, not_4_out, reset, WR_A, WR_B, WR_C, WR_D,
       WR_INC, WR_Inst, WR_J1, WR_J2, WR_M1, WR_M2, WR_PC, WR_Status, WR_X, WR_Y;
  wire [2:0] alu_1_z, Func, SelAddrReg, Status;
  wire [3:0] SelReg;
  wire [7:0] alu_1_result, bit_extender_1_out, bus_con_1_saida, instru, ram_1_dout, regb_1_const_out,
       regc_1_const_out;
  wire [15:0] adder_1_out, m_1_regm;

  StateMachine statemachine_1 (
    .Instruction(instru), .Status(Status), .Clk(clk), .reset(reset), .SelReg(SelReg),
    .SelAddrReg(SelAddrReg), .Func(Func),
    .WR({WR_A, WR_B, WR_C, WR_D, WR_M1, WR_M2, WR_X, WR_Y, WR_INC, WR_Inst, WR_PC, Mem, WR_J1, WR_J2, WR_Status}),
    .Bus_sel(Bus_sel));
  Clock clock_1 (.out(clk));
  POR por_1 (.out(reset));
  // Probe on SelAddrReg
  // Probe on Func
  not not_1 (not_1_out, SelReg[1]);
  // Probe on SelReg
  nand nand_1 (nand_1_out, SelReg[0], not_1_out);
  nand nand_2 (nand_2_out, SelReg[2], SelReg[3]);
  bus_con bus_con_1 (.enable(nor_1_out), .D(bit_extender_1_out), .Saida(bus_con_1_saida));
  assign bit_extender_1_out = {{3{instru[4]}}, instru[4:0]};  // Bit_Extender bit_extender_1
  nor nor_1 (nor_1_out, nand_1_out, nand_2_out);
  Adder #(.width(16)) adder_1 (.a(m_1_regm), .b(16'h1), .out(adder_1_out));  // open: cin, cout
  RegA rega_1 (
    .Data_In(bus_con_1_saida), .Sel(SelReg), .W_R(WR_A), .clk(clk), .reset(reset), .Data_Out(bus_con_1_saida));
  RegB regb_1 (
    .Data_In(bus_con_1_saida), .Sel(SelReg), .W_R(WR_B), .clk(clk), .reset(reset),
    .Data_Out(bus_con_1_saida), .const_out(regb_1_const_out));
  RegC regc_1 (
    .Data_In(bus_con_1_saida), .Sel(SelReg), .W_R(WR_C), .clk(clk), .reset(reset),
    .Data_Out(bus_con_1_saida), .const_out(regc_1_const_out));
  RegD regd_1 (
    .Data_In(bus_con_1_saida), .Sel(SelReg), .W_R(WR_D), .clk(clk), .reset(reset), .Data_Out(bus_con_1_saida));
  M m_1 (
    .Data_In(bus_con_1_saida), .Sel(SelReg), .Sel_Bus2(SelAddrReg), .W_R1(WR_M1), .W_R2(WR_M2), .clk(clk),
    .reset(reset), .Data_Out(bus_con_1_saida), .RegM(m_1_regm));
  XY2 xy2_1 (
    .Sel_Bus2(SelAddrReg), .bus_sel(Bus_sel), .Data_In(bus_con_1_saida), .W_R1(WR_X), .Data_In_16(m_1_regm),
    .clk(clk), .W_R2(WR_Y), .Sel(SelReg), .reset(reset), .Data_Out(bus_con_1_saida), .RegM(m_1_regm));
  J j_1 (
    .Data_In(bus_con_1_saida), .Sel(SelReg), .Sel_Bus2(SelAddrReg), .W_R1(WR_J1), .W_R2(WR_J2), .clk(clk),
    .reset(reset), .Data_Out(bus_con_1_saida), .RegM(m_1_regm));
  Inst inst_1 (.Data_In(bus_con_1_saida), .W_R(WR_Inst), .clk(clk), .reset(reset), .const_out(instru));
  PC pc_1 (.Sel_Bus2(SelAddrReg), .W_R1(WR_PC), .clk(clk), .reset(reset), .in_5(m_1_regm), .RegM(m_1_regm));
  Inc inc_1 (.Sel_Bus2(SelAddrReg), .W_R1(WR_INC), .clk(clk), .reset(reset), .in_5(adder_1_out), .RegM(m_1_regm));
  // Probe on instru
  Pull_Resistor #(.pull(1)) pull_resistor_1 (.node(bus_con_1_saida[0]));
  Pull_Resistor #(.pull(1)) pull_resistor_2 (.node(bus_con_1_saida[1]));
  Pull_Resistor #(.pull(1)) pull_resistor_3 (.node(bus_con_1_saida[2]));
  // Probe on bus_con_1_saida
  Pull_Resistor #(.pull(1)) pull_resistor_4 (.node(bus_con_1_saida[3]));
  Pull_Resistor #(.pull(1)) pull_resistor_5 (.node(bus_con_1_saida[4]));
  Pull_Resistor #(.pull(1)) pull_resistor_6 (.node(bus_con_1_saida[5]));
  Pull_Resistor #(.pull(1)) pull_resistor_7 (.node(bus_con_1_saida[6]));
  // Probe on m_1_regm
  RAM #(.addrWidth(16), .asyncread("true"), .\type ("nonvolatile")) ram_1 (
    .addr(m_1_regm), .we(Mem), .oe(1'b1), .clk(clk), .din(bus_con_1_saida), .dout(ram_1_dout));
  Pull_Resistor #(.pull(1)) pull_resistor_8 (.node(bus_con_1_saida[7]));
  not not_2 (not_2_out, SelReg[0]);
  nand nand_3 (nand_3_out, not_2_out, not_3_out);
  not not_3 (not_3_out, SelReg[1]);
  nand nand_4 (nand_4_out, SelReg[2], SelReg[3]);
  not not_4 (not_4_out, SelReg[2]);
  Pull_Resistor #(.pull(1)) pull_resistor_9 (.node(m_1_regm[0]));
  Pull_Resistor #(.pull(1)) pull_resistor_10 (.node(m_1_regm[1]));
  Pull_Resistor #(.pull(1)) pull_resistor_11 (.node(m_1_regm[2]));
  nor nor_2 (nor_2_out, nand_3_out, nand_4_out);
  ALU alu_1 (
    .func(Func), .B(regb_1_const_out), .C(regc_1_const_out), .Result(alu_1_result), .Z(alu_1_z[0]),
    .S(alu_1_z[1]), .Cy(alu_1_z[2]));
  bus_con bus_con_2 (.enable(nor_3_out), .D(ram_1_dout), .Saida(bus_con_1_saida));
  nand nand_5 (nand_5_out, SelReg[0], SelReg[1]);
  nand nand_6 (nand_6_out, not_4_out, SelReg[3]);
  Pull_Resistor #(.pull(1)) pull_resistor_12 (.node(m_1_regm[3]));
  Pull_Resistor #(.pull(1)) pull_resistor_13 (.node(m_1_regm[4]));
  Pull_Resistor #(.pull(1)) pull_resistor_14 (.node(m_1_regm[5]));
  Pull_Resistor #(.pull(1)) pull_resistor_15 (.node(m_1_regm[6]));
  nor nor_3 (nor_3_out, nand_5_out, nand_6_out);
  Pull_Resistor #(.pull(1)) pull_resistor_16 (.node(m_1_regm[7]));
  Pull_Resistor #(.pull(1)) pull_resistor_17 (.node(m_1_regm[8]));
  Pull_Resistor #(.pull(1)) pull_resistor_18 (.node(m_1_regm[9]));
  Pull_Resistor #(.pull(1)) pull_resistor_19 (.node(m_1_regm[10]));
  bus_con bus_con_3 (.enable(nor_2_out), .D(alu_1_result), .Saida(bus_con_1_saida));
  Register #(.width(3)) register_1 (.D(alu_1_z), .en(WR_Status), .clk(clk), .Q(Status));  // open: clr
  Pull_Resistor #(.pull(1)) pull_resistor_20 (.node(m_1_regm[11]));
  Pull_Resistor #(.pull(1)) pull_resistor_21 (.node(m_1_regm[12]));
  Pull_Resistor #(.pull(1)) pull_resistor_22 (.node(m_1_regm[13]));
  Pull_Resistor #(.pull(1)) pull_resistor_23 (.node(m_1_regm[14]));
  Pull_Resistor #(.pull(1)) pull_resistor_24 (.node(m_1_regm[15]));
endmodule

module ALU (
  input  [2:0] func,
  input  [7:0] B,
  input  [7:0] C,
  output [7:0] Result,
  output Z,
  output S,
  output Cy
);

  wire [7:0] adder_1_out, adder_2_out, and_1_out, not_1_out, or_1_out, shifter_1_out, xor_1_out;

  Adder adder_1 (.a(B), .b(C), .out(adder_1_out), .cout(Cy));  // open: cin
  Adder adder_2 (.a(B), .b(8'h1), .out(adder_2_out));  // open: cin, cout
  assign and_1_out = B & C;  // AND_Gate and_1, 8 bits wide
  assign or_1_out = B | C;  // OR_Gate or_1, 8 bits wide
  assign xor_1_out = B ^ C;  // XOR_Gate xor_1, 8 bits wide
  assign not_1_out = ~B;  // NOT_Gate not_1, 8 bits wide
  Shifter shifter_1 (.in(B), .\dist (C[2:0]), .out(shifter_1_out));
  Multiplexer #(.select(3), .width(8)) multiplexer_1 (
    .in0(adder_1_out), .in1(adder_2_out), .in2(and_1_out), .in3(or_1_out), .in4(xor_1_out), .in5(not_1_out),
    .in6(shifter_1_out), .out(Result), .sel(func));  // open: in7
  Comparator comparator_1 (.a(Result), .b({8{1'b0}}), .eq(Z));  // open: gt, lt

  assign S = Result[7];
endmodule

module StateMachine (
  input  [7:0] Instruction,
  input  [2:0] Status,
  input  Clk,
  input  reset,
  output [3:0] SelReg,
  output [2:0] SelAddrReg,
  output [2:0] Func,
  output [14:0] WR,
  output Bus_sel
);

  wire [4:0] register_1_q, statedecode_1_nextstate;

  // Probe on Instruction
  Register #(.width(5)) register_1 (.D(statedecode_1_nextstate), .clk(Clk), .Q(register_1_q), .clr(reset));  // open: en
  StateDecode statedecode_1 (
    .Status(Status), .Instru(Instruction), .State(register_1_q), .NextState(statedecode_1_nextstate),
    .SelReg(SelReg), .SelAddr(SelAddrReg), .Func(Func), .WR(WR), .busSel(Bus_sel));

  // Other names for the same wires on the sheet: inst[7:0] = Instruction; Stat[2:0] = Status
endmodule

module StateDecode (
  input  [2:0] Status,
  input  [7:0] Instru,
  input  [4:0] State,
  output [4:0] NextState,
  output [3:0] SelReg,
  output [2:0] SelAddr,
  output [2:0] Func,
  output [14:0] WR,
  output busSel
);

  wire pla_31_out, undriven;
  wire [2:0] pla_10_out, pla_13_out;
  wire [3:0] pla_6_out;
  wire [4:0] pla_1_out;
  wire [14:0] pla_16_out;

  // PlaRom #(.Contents("2 2 0 1 1 0 0 0 0 1 0 0 0 0 0 0 1 2 1 2 2 0 0 0 0 0 0 0 0 0 0 0 2 0 2 2 1 0 0 0 0 0 0 0 0 0 0 0 1 1 2 2 2 0 0 0 0 1 0 0 0 0 0 0 1 1 2 2 2 0 0 0 0 2 0 0 0 0 0 0 1 1 2 2 1 0 0 0 0 0 0 0 0 0 0 0 2 0 1 1 2 0 0 0 0 0 0 0 0 0 0 0 2 0 2 1 1 0 0 0 0 0 0 0 0 0 0 0 2 0 1 2 1 0 0 0 0 0 0 0 0 0 0 0 2 0 2 1 2 0 0 0 0 0 0 0 0 0 0 0 0 2 2 1 2 0 0 0 0 0 0 0 0 0 0 0 0 1 0 0 0 0 0 1 0 0 0 0 0 1 0 0 0 0 0 0 1 0 0 0 0 0 1 0 0 0 0 0 1 0 0 0 0 0 0 1 0 0 0 0 0 1 0 0 0 0 0 0 1 0 0 0 0 0 1 0 0 0 0 0 0 1"), .\and (11), .outputs(6)) plarom_1: pin names not known
  // PlaRom #(.Contents("1 1 1 2 2 2 0 2 0 2 2 2 0 0 0 0 1 1 1 2 2 2 1 2 2 0 0 0 0 0 0 0 1 1 1 2 2 2 0 2 0 0 1 2 0 0 0 0 1 1 1 2 2 2 0 2 1 0 0 1 0 0 0 0 1 1 1 2 2 2 2 0 0 0 0 2 1 0 0 0 2 0 1 2 2 0 0 0 1 1 1 0 0 0 0 1 2 0 1 2 2 0 0 0 1 1 2 0 0 0 0 2 2 2 0 2 2 0 0 0 1 1 1 0 0 0 0 2 2 2 0 2 2 0 0 0 1 1 2 0 0 0 0 1 1 1 1 2 2 2 2 2 0 0 0 1 0 0 0 0 1 1 1 2 2 2 0 1 2 0 0 0 0 0 0 0 1 1 1 2 2 2 0 2 0 0 0 0 2 0 0 0 1 1 1 2 2 2 0 1 1 0 0 0 0 0 0 0 2 0 1 2 2 0 0 0 1 2 0 0 0 2 0 0 2 2 0 2 2 0 0 0 1 2 0 0 0 1 0 0 1 1 1 2 2 1 1 0 0 0 0 0 0 0 0 0 1 1 1 2 2 1 2 0 0 0 0 0 0 0 0 0 2 0 1 1 1 0 0 0 0 2 0 0 0 0 0 0 2 0 1 2 2 0 0 0 2 0 0 0 0 0 2 0 2 2 0 2 2 0 0 0 2 0 0 0 0 0 1 0 2 1 1 1 1 0 0 0 0 0 0 0 0 0 0 0 2 1 1 2 2 0 0 0 0 0 0 0 0 0 0 0 1 1 1 2 1 0 0 0 0 0 0 0 0 0 0 0 1 2 0 2 1 0 0 0 0 0 0 0 0 0 0 0 2 0 1 1 2 0 0 0 0 0 0 0 0 0 0 0 1 1 1 2 1 0 0 0 0 0 0 0 0 0 0 0 2 0 2 1 1 0 0 0 0 0 0 0 0 0 0 0 2 0 1 2 1 0 0 0 0 0 0 0 0 0 0 0 0 2 2 2 2 0 0 0 0 0 0 0 0 0 0 0 2 0 2 1 2 0 0 0 0 0 0 0 0 0 0 0 1 1 2 1 2 0 0 2 2 2 0 0 0 0 0 0 1 0 0 0 1 0 0 0 1 0 0 0 1 0 0 0 1 0 0 0 1 0 0 0 1 0 0 0 1 0 0 0 1 0 0 0 1 0 0 0 1 0 0 0 1 0 0 0 1 0 0 0 1 0 0 0 1 0 0 0 1 0 0 0 1 0 0 0 1 0 0 0 1 0 0 0 1 0 0 0 1 0 0 0 1 0 0 0 0 1 0 0 0 0 1 0 0 0 1 0 0 0 1 0 0 0 1 0 0 0 1 0 0 0 1 0 0 0 1 0 0 0 0 1"), .\and (31), .outputs(4)) plarom_2: pin names not known
  // PlaRom #(.Contents("1 1 2 1 2 0 0 2 2 1 0 0 0 0 0 0 2 2 0 1 1 0 0 0 0 1 0 0 0 0 0 0 1 2 1 2 2 0 0 0 0 0 0 0 0 0 0 0 2 0 2 2 1 0 0 0 0 0 0 0 0 0 0 0 1 1 2 1 2 0 0 2 1 2 0 0 0 0 0 0 0 2 2 2 1 0 0 0 0 0 0 0 0 0 0 0 1 1 2 1 2 0 0 2 1 1 0 0 0 0 0 0 0 2 2 2 2 0 0 0 0 0 0 0 0 0 0 0 1 1 2 1 2 0 0 1 2 2 0 0 0 0 0 0 0 2 2 1 1 0 0 0 0 0 0 2 2 0 0 0 1 1 2 1 2 0 0 1 2 1 0 0 0 0 0 0 0 2 2 1 1 0 0 0 0 0 0 2 1 0 0 0 1 1 2 0 2 0 0 1 1 2 0 0 0 0 0 0 0 2 2 1 1 0 0 0 0 0 0 1 2 0 0 0 1 2 1 1 2 0 0 2 0 0 0 0 0 0 0 0 1 1 2 2 2 0 0 0 0 2 0 0 0 0 0 0 1 1 2 0 2 0 0 1 1 1 0 0 0 0 0 0 0 2 2 1 1 0 0 0 0 0 0 1 1 0 0 0 1 2 1 1 2 0 0 1 0 0 0 0 0 0 0 0 1 1 2 2 2 0 0 0 0 1 0 0 0 0 0 0 1 1 2 2 0 0 0 0 0 0 0 0 2 0 0 0 1 1 2 2 0 0 0 0 0 0 0 2 0 0 0 0 1 1 2 2 0 0 0 0 0 0 2 0 0 0 0 0 2 2 0 1 0 0 0 0 0 0 1 2 0 0 0 0 1 2 0 2 1 0 0 0 0 0 0 0 0 0 0 0 1 1 1 2 1 0 0 0 0 0 0 0 0 0 0 0 2 0 2 1 1 0 0 0 0 0 0 0 0 0 0 0 2 2 0 1 2 0 0 0 0 0 0 0 0 0 0 0 0 1 1 1 2 0 0 0 0 0 0 0 0 0 0 0 1 0 0 0 0 0 0 0 0 0 0 1 0 0 0 0 0 0 0 0 0 0 1 0 0 0 0 0 0 0 0 0 0 1 0 0 0 0 0 0 0 0 0 0 0 1 0 0 0 0 0 0 0 0 0 0 1 0 0 0 0 0 0 0 0 0 0 0 1 0 0 0 0 0 0 0 0 0 0 1 0 0 0 0 0 0 0 0 0 0 0 1 0 0 0 0 0 0 0 0 0 0 1 0 0 0 0 0 0 0 0 0 0 0 1 0 0 0 0 0 0 0 0 0 0 1 0 0 0 0 0 0 0 0 0 0 0 1 0 0 0 0 0 0 0 0 0 0 1 0 0 0 0 0 0 0 0 0 0 1 0 0 0 0 0 0 0 0 0 0 1 0 0 0 0 0 0 0 0 0 0 0 1 0 0 0 0 0 0 0 0 0 0 1 0 0 0 0 0 0 0 0 0 0 1 0 0 0 0 0 0 0 0 0 0 1 0 0 0 0 0 0 0 0 0 0 0 1 0 0 0 0 0 0 0 0 0 0 0 1 0 0 0 0 0 0 0 0 0 0 0 1 0 0 0 0 0 0 0 0 0 0 0 1 0 0 0 0 0 0 0 0 0 0 1 0 0 0 0 0 0 0 0 0 0 1 0 0 0 0 0 0 0 0 0 0 1 0 0 0 0 0 0 0 0 0 0 1 0 0 0 0 0 0 0 0 0 0 1"), .\and (29), .outputs(11)) plarom_3: pin names not known
  // PlaRom #(.Contents("2 0 1 2 2 0 0 0 1 1 1 0 0 0 0 1 2 0 1 2 2 0 0 0 1 1 2 0 0 0 0 2 2 0 1 2 2 0 0 0 1 2 0 0 0 2 0 0 2 2 0 1 0 0 0 0 0 0 2 1 0 0 0 0 2 0 1 2 2 0 0 0 2 0 0 0 0 0 2 0 1 1 1 2 1 0 0 0 0 0 0 0 0 0 0 0 0 2 2 2 1 0 0 0 0 0 0 0 0 0 0 0 2 0 2 1 1 0 0 0 0 0 0 0 0 0 0 0 2 2 0 1 2 0 0 0 0 0 0 0 0 0 0 0 2 1 1 2 2 0 0 0 0 0 0 0 0 0 0 0 0 1 1 1 2 0 0 0 0 0 0 0 0 0 0 0 1 1 1 2 2 2 0 2 0 2 2 2 0 0 0 0 1 1 1 2 2 2 1 2 2 0 0 0 0 0 0 0 1 1 1 2 2 2 0 2 0 0 1 2 0 0 0 0 1 1 1 2 2 2 0 2 1 0 0 1 0 0 0 0 1 1 1 2 2 2 2 0 0 0 0 2 1 0 0 0 2 2 0 2 2 0 0 0 1 1 1 0 0 0 0 2 2 2 0 2 2 0 0 0 1 1 2 0 0 0 0 1 1 1 1 2 2 2 2 2 0 0 0 1 0 0 0 0 1 1 1 2 2 2 0 1 2 0 0 0 0 0 0 0 1 1 1 2 2 2 0 2 0 0 0 0 2 0 0 0 1 1 1 2 2 2 0 1 1 0 0 0 0 0 0 0 2 2 0 2 2 0 0 0 1 2 0 0 0 1 0 0 1 1 1 2 2 1 1 0 0 0 0 0 0 0 0 0 1 1 1 2 2 1 2 0 0 0 0 0 0 0 0 0 2 2 0 2 2 0 0 0 2 0 0 0 0 0 1 0 2 1 1 1 1 0 0 0 0 0 0 0 0 0 0 0 1 2 1 2 2 0 0 0 0 0 0 0 0 0 0 0 2 0 2 2 1 0 0 0 0 0 0 0 0 0 0 0 2 0 1 2 1 0 0 0 0 0 0 0 0 0 0 0 0 2 2 2 2 0 0 0 0 0 0 0 0 0 0 0 2 0 2 1 2 0 0 0 0 0 0 0 0 0 0 0 1 0 1 0 1 0 1 0 1 0 1 0 1 0 1 0 1 0 1 0 1 0 0 1 0 1 0 1 0 1 0 1 0 1 0 1 0 1 0 1 0 1 0 1 0 1 0 1 0 1 0 1 0 1 0 1 0 1 0 1 0 1 0 1"), .\and (32), .outputs(2)) plarom_4: pin names not known
  // PlaRom #(.Contents("0 2 2 1 1 0 0 0 0 0 0 2 1 0 0 0 0 2 2 1 1 0 0 0 0 0 0 1 1 0 0 0 1 2 1 1 2 0 0 1 0 0 0 0 0 0 0 0 1 2 1 1 2 0 0 2 0 0 0 0 0 0 0 0 1 2 1 1 1 0 0 0 0 0 0 0 0 0 0 0 0 0 2 1 0 0 0 0 0 0 0 0 2 0 0 0 1 1 1 2 1 0 0 0 0 0 0 0 0 0 0 0 0 2 2 2 1 0 0 0 0 0 0 0 0 0 0 0 2 0 2 1 1 0 0 0 0 0 0 0 0 0 0 0 2 2 0 1 2 0 0 0 0 0 0 0 0 0 0 0 2 1 1 2 2 0 0 0 0 0 0 0 0 0 0 0 0 1 1 1 2 0 0 0 0 0 0 0 0 0 0 0 2 0 1 2 1 0 0 0 0 0 0 0 0 0 0 0 0 2 2 2 2 0 0 0 0 0 0 0 0 0 0 0 2 0 2 1 2 0 0 0 0 0 0 0 0 0 0 0 0 2 2 1 1 0 0 0 0 0 0 1 2 0 0 0 0 2 2 1 1 0 0 0 0 0 0 1 1 0 0 0 0 0 2 1 0 0 0 0 0 0 0 2 0 0 0 0 1 1 1 2 1 0 0 0 0 0 0 0 0 0 0 0 0 2 2 2 1 0 0 0 0 0 0 0 0 0 0 0 2 0 2 1 1 0 0 0 0 0 0 0 0 0 0 0 2 2 0 1 2 0 0 0 0 0 0 0 0 0 0 0 2 1 1 2 2 0 0 0 0 0 0 0 0 0 0 0 0 1 1 1 2 0 0 0 0 0 0 0 0 0 0 0 2 0 1 2 1 0 0 0 0 0 0 0 0 0 0 0 0 2 2 2 2 0 0 0 0 0 0 0 0 0 0 0 2 0 2 1 2 0 0 0 0 0 0 0 0 0 0 0 1 0 1 0 1 0 1 0 1 0 1 0 1 0 1 0 1 0 1 0 1 0 1 0 1 0 1 0 1 0 0 1 0 1 0 1 0 1 0 1 0 1 0 1 0 1 0 1 0 1 0 1 0 1"), .\and (27), .outputs(2)) plarom_5: pin names not known
  // PlaRom #(.Contents("1 2 1 1 2 0 0 1 0 0 0 0 0 0 0 0 1 2 1 1 2 0 0 2 0 0 0 0 0 0 0 0 1 1 2 0 0 0 0 0 0 0 2 0 0 0 0 0 1 1 2 2 2 0 0 0 0 1 0 0 0 0 0 0 1 1 2 2 2 0 0 0 0 2 0 0 0 0 0 0 1 2 1 1 1 0 0 0 0 0 0 0 0 0 0 0 1 1 2 2 1 0 0 0 0 0 0 0 0 0 0 0 0 2 2 1 1 0 0 0 0 0 0 2 2 0 0 0 0 2 2 1 1 0 0 0 0 0 0 1 2 0 0 0 0 2 2 1 1 0 0 0 0 0 0 2 1 0 0 0 0 2 2 1 1 0 0 0 0 0 0 1 1 0 0 0 1 2 1 1 2 0 0 1 0 0 0 0 0 0 0 0 1 2 1 1 2 0 0 2 0 0 0 0 0 0 0 0 1 1 2 2 2 0 0 0 0 1 0 0 0 0 0 0 1 1 2 2 2 0 0 0 0 2 0 0 0 0 0 0 1 2 1 1 1 0 0 0 0 0 0 0 0 0 0 0 1 1 2 2 1 0 0 0 0 0 0 0 0 0 0 0 1 1 1 2 1 0 0 0 0 0 0 0 0 0 0 0 0 2 2 2 1 0 0 0 0 0 0 0 0 0 0 0 2 0 2 1 1 0 0 0 0 0 0 0 0 0 0 0 2 2 0 1 2 0 0 0 0 0 0 0 0 0 0 0 2 1 1 2 2 0 0 0 0 0 0 0 0 0 0 0 0 1 1 1 2 0 0 0 0 0 0 0 0 0 0 0 2 0 1 2 1 0 0 0 0 0 0 0 0 0 0 0 0 2 2 2 2 0 0 0 0 0 0 0 0 0 0 0 2 0 2 1 2 0 0 0 0 0 0 0 0 0 0 0 1 0 1 0 1 0 1 0 1 0 1 0 1 0 0 1 0 1 0 1 0 1 0 1 0 1 0 1 0 1 0 1 0 1 0 1 0 1 0 1 0 1 0 1 0 1 0 1 0 1 0 1"), .\and (26), .outputs(2)) plarom_6: pin names not known
  // PlaRom #(.Contents("1 1 1 2 2 2 0 2 0 2 2 2 0 0 0 0 1 1 1 2 2 2 2 0 0 0 0 2 1 0 0 0 2 0 1 2 2 0 0 0 1 1 1 0 0 0 0 1 2 0 1 2 2 0 0 0 1 1 2 0 0 0 0 2 1 1 2 1 2 0 0 1 2 1 0 0 0 0 0 0 1 1 2 1 2 0 0 1 2 2 0 0 0 0 0 0 2 2 0 2 2 0 0 0 1 1 1 0 0 0 0 2 1 1 2 1 2 0 0 2 2 2 0 0 0 0 0 0 2 2 0 2 2 0 0 0 1 1 2 0 0 0 0 1 1 1 2 1 2 0 0 2 2 1 0 0 0 0 0 0 1 1 2 1 2 0 0 2 1 1 0 0 0 0 0 0 1 1 2 1 2 0 0 2 1 2 0 0 0 0 0 0 1 1 1 2 2 2 2 2 0 0 0 1 0 0 0 0 1 1 2 0 2 0 0 1 1 1 0 0 0 0 0 0 1 1 2 0 2 0 0 1 1 2 0 0 0 0 0 0 2 0 1 2 2 0 0 0 1 2 0 0 0 2 0 0 2 2 0 2 2 0 0 0 1 2 0 0 0 1 0 0 0 0 1 2 0 2 0 0 2 2 0 0 0 0 0 0 2 0 1 2 2 0 0 0 2 0 0 0 0 0 2 0 2 2 0 2 2 0 0 0 2 0 0 0 0 0 1 0 1 2 1 1 2 0 0 1 0 0 0 0 0 0 0 0 1 2 1 1 2 0 0 2 0 0 0 0 0 0 0 0 1 1 2 2 2 0 0 0 0 1 0 0 0 0 0 0 1 1 2 2 2 0 0 0 0 2 0 0 0 0 0 0 0 2 2 1 2 0 0 0 0 0 0 0 0 0 0 0 1 2 1 2 2 0 0 0 0 0 0 0 0 0 0 0 2 0 2 2 2 0 0 0 0 0 0 0 0 0 0 0 2 1 1 2 2 0 0 0 0 0 0 0 0 0 0 0 0 0 0 0 1 0 0 0 0 0 0 0 0 0 0 0 1 1 1 1 1 1 1 1 1 1 1 1 1 1 1 1 1 1 1 1 1 1 1 1 1 1 1 1 1"), .\and (29), .outputs(1)) plarom_7: pin names not known
  // PlaRom #(.Contents("1 1 1 2 2 2 0 2 0 2 2 2 0 0 0 0 1 1 1 2 2 2 1 2 2 0 0 0 0 0 0 0 1 1 1 2 2 2 0 1 1 0 0 0 0 0 0 0 1 1 2 2 1 0 0 0 0 0 0 0 0 0 0 0 1 2 0 2 1 0 0 0 0 0 0 0 0 0 0 0 2 0 2 2 1 0 0 0 0 0 0 0 0 0 0 0 1 1 1 2 1 0 0 0 0 0 0 0 0 0 0 0 2 0 2 2 2 0 0 0 0 0 0 0 0 0 0 0 2 2 0 1 2 0 0 0 0 0 0 0 0 0 0 0 0 1 1 1 2 0 0 0 0 0 0 0 0 0 0 0 2 0 1 2 1 0 0 0 0 0 0 0 0 0 0 0 2 0 2 1 2 0 0 0 0 0 0 0 0 0 0 0 1 1 1 2 2 2 0 2 0 2 2 2 0 0 0 0 1 1 1 2 2 2 0 1 2 0 0 0 0 0 0 0 1 1 1 2 2 2 0 2 0 0 0 0 2 0 0 0 1 1 1 2 2 2 0 1 1 0 0 0 0 0 0 0 1 1 1 2 2 1 1 0 0 0 0 0 0 0 0 0 0 1 2 1 1 0 0 0 0 0 0 0 0 0 0 0 1 1 2 2 1 0 0 0 0 0 0 0 0 0 0 0 0 2 2 2 1 0 0 0 0 0 0 0 0 0 0 0 2 0 2 2 2 0 0 0 0 0 0 0 0 0 0 0 2 0 2 1 2 0 0 0 0 0 0 0 0 0 0 0 1 1 1 2 2 2 1 2 2 0 0 0 0 0 0 0 1 1 1 2 2 2 0 2 0 0 1 2 0 0 0 0 1 1 1 2 2 2 0 2 1 0 0 1 0 0 0 0 1 1 1 2 2 2 2 2 0 0 0 1 0 0 0 0 1 1 1 2 2 0 2 1 0 0 0 0 0 0 0 0 1 1 1 2 2 2 0 1 2 0 0 0 0 0 0 0 1 1 1 2 2 1 2 0 0 0 0 0 0 0 0 0 1 2 1 1 1 0 0 0 0 0 0 0 0 0 0 0 0 2 0 2 1 0 0 0 0 0 0 0 0 0 0 0 2 2 0 1 2 0 0 0 0 0 0 0 0 0 0 0 1 0 0 1 0 0 1 0 0 1 0 0 1 0 0 1 0 0 1 0 0 1 0 0 1 0 0 1 0 0 1 0 0 1 0 0 0 1 0 0 1 0 0 1 0 0 1 0 0 1 0 0 1 0 0 1 0 0 1 0 0 1 0 0 1 0 0 0 1 0 0 1 0 0 1 0 0 1 0 0 1 0 0 1 0 0 1 0 0 1 0 0 1 0 0 1"), .\and (32), .outputs(3)) plarom_8: pin names not known
  // PlaRom #(.Contents("1 1 1 2 2 2 0 2 0 2 2 2 0 0 0 0 1 1 1 2 2 2 0 2 0 0 1 2 0 0 0 0 1 1 1 2 2 2 0 2 1 0 0 1 0 0 0 0 1 1 1 2 2 2 2 0 0 0 0 2 1 0 0 0 1 1 1 2 2 2 2 2 0 0 0 1 0 0 0 0 1 1 1 2 2 2 0 2 0 0 0 0 2 0 0 0 2 0 1 1 2 0 0 0 0 0 0 0 0 0 0 0 2 0 2 2 1 0 0 0 0 0 0 0 0 0 0 0 2 0 2 1 1 0 0 0 0 0 0 0 0 0 0 0 2 0 2 2 2 0 0 0 0 0 0 0 0 0 0 0 2 0 1 2 1 0 0 0 0 0 0 0 0 0 0 0 0 2 2 2 2 0 0 0 0 0 0 0 0 0 0 0 2 0 2 1 2 0 0 0 0 0 0 0 0 0 0 0 1 1 1 1 1 1 1 1 1 1 1 1 1"), .\and (13), .outputs(1)) plarom_9: pin names not known
  PLA #(.in_width(16), .out_width(1), .\table ("xx01x1x1xx110xxx 1\nxx01x11x1xxxxxxx 1\nxx01x1xx11xxxxxx 1\n01x0xxxxxxxxxxxx 1\nx101xxxxxxxxxxxx 1\n001xxxxxxxxxxxxx 1\n1xx1xxxxxxxxxxxx 1\nxxxx0xxxxxxxxxxx 1")) pla_1 (
    .in(undriven), .out(pla_1_out[0]));
  PLA #(.in_width(16), .out_width(1), .\table ("000x11011xxxxxxx 1\n000x11xxx111xxxx 1\n000x11x00xxxxxxx 1\n1x1x1xxxxxxxxxxx 1\nxxx10xxxxxxxxxxx 1\n1xx01xxxxxxxxxxx 1\nx0001xxxxxxxxxxx 1")) pla_2 (
    .in(undriven), .out(pla_1_out[1]));
  PLA #(.in_width(16), .out_width(1), .\table ("00011x0xxx11xxxx 1\n000111x0xxxxxxxx 1\n1x10xxxxxxxxxxxx 1\nx1110xxxxxxxxxxx 1\n001x0xxxxxxxxxxx 1\n000111xxxxxx1xxx 1\n0001100xxxxxxxxx 1\n1x1x1xxxxxxxxxxx 1")) pla_3 (
    .in(undriven), .out(pla_1_out[2]));
  PLA #(.in_width(16), .out_width(1), .\table ("00011x1xxxx0xxxx 1\n000111x1xx0xxxxx 1\n000111x1xxx0xxxx 1\n000111xx1xxxxxxx 1\n11x01xxxxxxxxxxx 1\nx1x10xxxxxxxxxxx 1\n010x0xxxxxxxxxxx 1\n0001101xxxxxxxxx 1")) pla_4 (
    .in(undriven), .out(pla_1_out[3]));
  PLA #(.in_width(16), .out_width(1), .\table ("0001111x1xxxxxxx 1\n000111x10xxxxxxx 1\n1x1xxxxxxxxxxxxx 1\n1xx10xxxxxxxxxxx 1\n1xx01xxxxxxxxxxx 1\nx1111xxxxxxxxxxx 1")) pla_5 (
    .in(undriven), .out(pla_1_out[4]));
  PLA #(.in_width(16), .out_width(1), .\table ("100x1xxxxxxxxxxx 1\n01x00xxxxxxxxxxx 1\n1x010xxxxxxxxxxx 1\nxx10xxxxxxxx1xxx 1\nx0010xxxxxxxxxxx 1\nxx001xxxxxxxxxxx 1\nx111xxxxxxxxxxxx 1\n1x10xxxxxxxxxxxx 1")) pla_6 (
    .in(undriven), .out(pla_6_out[0]));
  PLA #(.in_width(16), .out_width(1), .\table ("1x010xxxxxxxxxxx 1\n100x1xxxxxxxxxxx 1\nxx10xxxxxxx1xxxx 1\nx11x0xxxxxxxxxxx 1\n1xx01xxxxxxxxxxx 1\nx0010xxxxxxxxxxx 1\nx111xxxxxxxxxxxx 1\n1x10xxxxxxxxxxxx 1\nx0001xxxxxxxxxxx 1")) pla_7 (
    .in(undriven), .out(pla_6_out[1]));
  PLA #(.in_width(16), .out_width(1), .\table ("001xxxxxxx1xxxxx 1\n0011xxxxxxxxxxxx 1\n0100xxxxxxxxxxxx 1")) pla_8 (
    .in(undriven), .out(pla_6_out[2]));
  PLA #(.in_width(16), .out_width(1), .\table ("01x00xxxxxxxxxxx 1\n100x1xxxxxxxxxxx 1\n1x010xxxxxxxxxxx 1\nx0010xxxxxxxxxxx 1\n0x11xxxxxxxxxxxx 1\nxx001xxxxxxxxxxx 1\n1x10xxxxxxxxxxxx 1")) pla_9 (
    .in(undriven), .out(pla_6_out[3]));
  PLA #(.in_width(16), .out_width(1), .\table ("x1110xxxxxxxxxxx 1\n1x001xxxxxxxxxxx 1\n11x0xxxxxx01xxxx 1\n1x100xxxxxxxxxxx 1\n0x010xxxxxxxxxxx 1\nx0001xxxxxxxxxxx 1")) pla_10 (
    .in(undriven), .out(pla_10_out[0]));
  PLA #(.in_width(16), .out_width(1), .\table ("1x0x1xxx000xxxx0 1\n1x0x1xxx001xxxx1 1\n1x0x1xxx01xxx1xx 1\n1x0x1xxx1xxxxx1x 1\n1x001xxxxxxxxxxx 1\n11x0xxxxxx10xxxx 1\nx1110xxxxxxxxxxx 1\n1x100xxxxxxxxxxx 1\n00010xxxxxxxxxxx 1\nx0001xxxxxxxxxxx 1\n100x1xxxxxxxxxxx 1")) pla_11 (
    .in(undriven), .out(pla_10_out[1]));
  PLA #(.in_width(16), .out_width(1), .\table ("x1x11xxx000xxxx1 1\nx1x11xxx001xxxx0 1\nx1x11xxx01xxx0xx 1\nx1x11xxx1xxxxx0x 1\nx1111xxxxxxxxxxx 1\n0x011xxxxxxxxxxx 1\n1x101xxxxxxxxxxx 1\n100x0xxxxxxxxxxx 1\n1xx10xxxxxxxxxxx 1")) pla_12 (
    .in(undriven), .out(pla_10_out[2]));
  PLA #(.in_width(16), .out_width(1), .\table ("0011xxxxxxxx1xxx 1")) pla_13 (.in(undriven), .out(pla_13_out[0]));
  PLA #(.in_width(16), .out_width(1), .\table ("0011xxxxxxx1xxxx 1")) pla_14 (.in(undriven), .out(pla_13_out[1]));
  PLA #(.in_width(16), .out_width(1), .\table ("0011xxxxxx1xxxxx 1")) pla_15 (.in(undriven), .out(pla_13_out[2]));
  PLA #(.in_width(16), .out_width(1), .\table ("0011xxxxxxxxxxxx 1")) pla_16 (.in(undriven), .out(pla_16_out[0]));
  PLA #(.in_width(16), .out_width(1), .\table ("1x100xxxxxxxxxxx 1\n1x001xxxxxxxxxxx 1")) pla_17 (
    .in(undriven), .out(pla_16_out[1]));
  PLA #(.in_width(16), .out_width(1), .\table ("1x101xxxxxxxxxxx 1\n1x010xxxxxxxxxxx 1")) pla_18 (
    .in(undriven), .out(pla_16_out[2]));
  PLA #(.in_width(16), .out_width(1), .\table ("x1101xxxxxxxxxxx 1")) pla_19 (.in(undriven), .out(pla_16_out[3]));
  PLA #(.in_width(16), .out_width(1), .\table ("1x000xxxx1xxxxxx 1\n1x011xxxxxxxxxxx 1\nx0011xxxxxxxxxxx 1\n10000xxxxxxxxxxx 1")) pla_20 (
    .in(undriven), .out(pla_16_out[4]));
  PLA #(.in_width(16), .out_width(1), .\table ("00010xxxxxxxxxxx 1")) pla_21 (.in(undriven), .out(pla_16_out[5]));
  PLA #(.in_width(16), .out_width(1), .\table ("1xx01xxxxxxxxxxx 1\nx111xxxxxxxxxxxx 1\n1x10xxxxxxxxxxxx 1\nxx010xxxxxxxxxxx 1")) pla_22 (
    .in(undriven), .out(pla_16_out[6]));
  PLA #(.in_width(16), .out_width(1), .\table ("00101xx111xxxxxx 1")) pla_23 (.in(undriven), .out(pla_16_out[7]));
  PLA #(.in_width(16), .out_width(1), .\table ("00101xx110xxxxxx 1\n11x00xxxx0xxxxxx 1\n1x110xxxxxxxxxxx 1\n01011xxxxxxxxxxx 1")) pla_24 (
    .in(undriven), .out(pla_16_out[8]));
  PLA #(.in_width(16), .out_width(1), .\table ("x1110xxxxxxxxxxx 1\n00101xx101xxxxxx 1")) pla_25 (
    .in(undriven), .out(pla_16_out[9]));
  PLA #(.in_width(16), .out_width(1), .\table ("00101xx100xxxxxx 1\nx1111xxxxxxxxxxx 1")) pla_26 (
    .in(undriven), .out(pla_16_out[10]));
  PLA #(.in_width(16), .out_width(1), .\table ("x1100xxxxxx11xxx 1\n00101xx011xxxxxx 1")) pla_27 (
    .in(undriven), .out(pla_16_out[11]));
  PLA #(.in_width(16), .out_width(1), .\table ("x1100xxxxxx10xxx 1\n00101xx010xxxxxx 1")) pla_28 (
    .in(undriven), .out(pla_16_out[12]));
  PLA #(.in_width(16), .out_width(1), .\table ("001x1xx001xxxxxx 1\nx1100xxxxxx01xxx 1\n01001xx1xxxxxxxx 1\n00111xxxx1xxxxxx 1")) pla_29 (
    .in(undriven), .out(pla_16_out[13]));
  PLA #(.in_width(16), .out_width(1), .\table ("001x1xx000xxxxxx 1\nx1100xxxxxx00xxx 1\n01001xx0xxxxxxxx 1\n00111xxxx0xxxxxx 1")) pla_30 (
    .in(undriven), .out(pla_16_out[14]));
  PLA #(.in_width(16), .out_width(1), .\table ("11x00xxxx0xxxxxx 1\n1x110xxxxxxxxxxx 1\n01011xxxxxxxxxxx 1")) pla_31 (
    .in(undriven), .out(pla_31_out));
endmodule
