// Logisim project logic_gates.circ as structural Verilog: 3 circuits, main circuit V_NAND
module V_NAND (
  input  A,
  input  B,
  output O
);

  wire transistor_2_out;

  Pull_Resistor #(.pull(1)) pull_resistor_1 (.node(O));
  Transistor #(.\type ("n")) transistor_1 (.in(transistor_2_out), .out(O), .gate(A));
  Transistor #(.\type ("n")) transistor_2 (.in(1'b0), .out(transistor_2_out), .gate(B));

  // Notes on the sheet:
  //   O: pull=up
endmodule

module V_NOT (
  input  A,
  output O
);

  Pull_Resistor #(.pull(1)) pull_resistor_1 (.node(O));
  Transistor #(.\type ("n")) transistor_1 (.in(1'b0), .out(O), .gate(A));
endmodule

module V_NOR (
  input  A,
  input  B,
  output O
);

  Pull_Resistor #(.pull(1)) pull_resistor_1 (.node(O));
  Transistor #(.\type ("n")) transistor_1 (.in(1'b0), .out(O), .gate(A));
  Transistor #(.\type ("n")) transistor_2 (.in(1'b0), .out(O), .gate(B));
endmodule
