// Logisim project registers.circ as structural Verilog: 22 circuits, main circuit bus_con
module XY2 (
  input  [2:0] Sel_Bus2,
  input  bus_sel,
  input  [7:0] Data_In,
  input  W_R1,
  input  [15:0] Data_In_16,
  input  clk,
  input  W_R2,
  input  [3:0] Sel,
  input  reset,
  output [7:0] Data_Out,
  output [15:0] RegM
);

  wire and_1_out, nand_1_out, nor_1_out, not_1_out, or_1_out;
  wire [7:0] multiplexer_1_out, multiplexer_2_out, x_1_data_out2, y_1_data_out2;

  and and_1 (and_1_out, W_R1, bus_sel);
  not not_1 (not_1_out, Sel_Bus2[1]);
  Multiplexer #(.width(8)) multiplexer_1 (.in0(Data_In), .in1(Data_In_16[7:0]), .out(multiplexer_1_out), .sel(bus_sel));
  Multiplexer #(.width(8)) multiplexer_2 (
    .in0(Data_In), .in1(Data_In_16[15:8]), .out(multiplexer_2_out), .sel(bus_sel));
  or or_1 (or_1_out, W_R2, and_1_out);
  nand nand_1 (nand_1_out, Sel_Bus2[0], not_1_out);
  nor nor_1 (nor_1_out, nand_1_out, Sel_Bus2[2]);
  X x_1 (
    .Data_In(multiplexer_1_out), .Sel(Sel), .W_R(W_R1), .clk(clk), .reset(reset), .Data_Out(Data_Out),
    .Data_out2(x_1_data_out2));
  Y y_1 (
    .Data_In(multiplexer_2_out), .Sel(Sel), .W_R(or_1_out), .clk(clk), .reset(reset), .Data_Out(Data_Out),
    .Data_out2(y_1_data_out2));
  bus_con_16 bus_con_16_1 (.Enable(nor_1_out), .Entrada({y_1_data_out2, x_1_data_out2}), .Saida(RegM));

  // Other names for the same wires on the sheet: D_in8[7:0] = Data_In; D_in16A[7:0] = Data_In_16[7:0];
  //   D_in16B[7:0] = Data_In_16[15:8]; WR1 = W_R1

  // Notes on the sheet:
  //   Data_In: pull=down
  //   Data_In_16: pull=down
endmodule

module RegA (
  input  [7:0] Data_In,
  input  [3:0] Sel,
  input  W_R,
  input  clk,
  input  reset,
  output [7:0] Data_Out
);

  wire nand_1_out, nand_2_out, nor_1_out, not_1_out, not_2_out, not_3_out, not_4_out;

  not not_1 (not_1_out, Sel[0]);
  not not_2 (not_2_out, Sel[1]);
  not not_3 (not_3_out, Sel[2]);
  not not_4 (not_4_out, Sel[3]);
  nand nand_1 (nand_1_out, not_1_out, not_2_out);
  nand nand_2 (nand_2_out, not_3_out, not_4_out);
  nor nor_1 (nor_1_out, nand_1_out, nand_2_out);
  RegBase regbase_1 (
    .enable(nor_1_out), .Data_In(Data_In), .W_R(W_R), .clk(clk), .reset(reset), .Data_Out(Data_Out));  // open: Data_out_allways
endmodule

module RegB (
  input  [7:0] Data_In,
  input  [3:0] Sel,
  input  W_R,
  input  clk,
  input  reset,
  output [7:0] Data_Out,
  output [7:0] const_out
);

  wire nand_1_out, nand_2_out, nor_1_out, not_1_out, not_2_out, not_3_out;

  not not_1 (not_1_out, Sel[1]);
  not not_2 (not_2_out, Sel[2]);
  not not_3 (not_3_out, Sel[3]);
  nand nand_1 (nand_1_out, Sel[0], not_1_out);
  nand nand_2 (nand_2_out, not_2_out, not_3_out);
  nor nor_1 (nor_1_out, nand_1_out, nand_2_out);
  RegBase regbase_1 (
    .enable(nor_1_out), .Data_In(Data_In), .W_R(W_R), .clk(clk), .reset(reset), .Data_Out(Data_Out),
    .Data_out_allways(const_out));
endmodule

module RegC (
  input  [7:0] Data_In,
  input  [3:0] Sel,
  input  W_R,
  input  clk,
  input  reset,
  output [7:0] Data_Out,
  output [7:0] const_out
);

  wire nand_1_out, nand_2_out, nor_1_out, not_1_out, not_2_out, not_3_out;

  not not_1 (not_1_out, Sel[0]);
  not not_2 (not_2_out, Sel[2]);
  not not_3 (not_3_out, Sel[3]);
  nand nand_1 (nand_1_out, not_1_out, Sel[1]);
  nand nand_2 (nand_2_out, not_2_out, not_3_out);
  nor nor_1 (nor_1_out, nand_1_out, nand_2_out);
  RegBase regbase_1 (
    .enable(nor_1_out), .Data_In(Data_In), .W_R(W_R), .clk(clk), .reset(reset), .Data_Out(Data_Out),
    .Data_out_allways(const_out));
endmodule

module RegD (
  input  [7:0] Data_In,
  input  [3:0] Sel,
  input  W_R,
  input  clk,
  input  reset,
  output [7:0] Data_Out
);

  wire nand_1_out, nand_2_out, nor_1_out, not_1_out, not_2_out;

  not not_1 (not_1_out, Sel[2]);
  not not_2 (not_2_out, Sel[3]);
  nand nand_1 (nand_1_out, Sel[0], Sel[1]);
  nand nand_2 (nand_2_out, not_1_out, not_2_out);
  nor nor_1 (nor_1_out, nand_1_out, nand_2_out);
  RegBase regbase_1 (
    .enable(nor_1_out), .Data_In(Data_In), .W_R(W_R), .clk(clk), .reset(reset), .Data_Out(Data_Out));  // open: Data_out_allways
endmodule

module M1 (
  input  [7:0] Data_In,
  input  [3:0] Sel,
  input  W_R,
  input  clk,
  input  reset,
  output [7:0] Data_Out,
  output [7:0] Data_out2
);

  wire nand_1_out, nand_2_out, nor_1_out, not_1_out, not_2_out, not_3_out;

  not not_1 (not_1_out, Sel[0]);
  not not_2 (not_2_out, Sel[1]);
  not not_3 (not_3_out, Sel[3]);
  nand nand_1 (nand_1_out, not_1_out, not_2_out);
  nand nand_2 (nand_2_out, Sel[2], not_3_out);
  nor nor_1 (nor_1_out, nand_1_out, nand_2_out);
  RegBase regbase_1 (
    .enable(nor_1_out), .Data_In(Data_In), .W_R(W_R), .clk(clk), .reset(reset), .Data_Out(Data_Out),
    .Data_out_allways(Data_out2));

  // Notes on the sheet:
  //   Data_In: pull=down
endmodule

module M2 (
  input  [7:0] Data_In,
  input  [3:0] Sel,
  input  W_R,
  input  clk,
  input  reset,
  output [7:0] Data_Out,
  output [7:0] Data_out2
);

  wire nand_1_out, nand_2_out, nor_1_out, not_1_out, not_2_out;

  not not_1 (not_1_out, Sel[1]);
  not not_2 (not_2_out, Sel[3]);
  nand nand_1 (nand_1_out, Sel[0], not_1_out);
  nand nand_2 (nand_2_out, Sel[2], not_2_out);
  nor nor_1 (nor_1_out, nand_1_out, nand_2_out);
  RegBase regbase_1 (
    .enable(nor_1_out), .Data_In(Data_In), .W_R(W_R), .clk(clk), .reset(reset), .Data_Out(Data_Out),
    .Data_out_allways(Data_out2));

  // Notes on the sheet:
  //   Data_In: pull=down
endmodule

module M (
  input  [7:0] Data_In,
  input  [3:0] Sel,
  input  [2:0] Sel_Bus2,
  input  W_R1,
  input  W_R2,
  input  clk,
  input  reset,
  output [7:0] Data_Out,
  output [15:0] RegM
);

  wire nand_1_out, nor_1_out, not_1_out, not_2_out;
  wire [7:0] m1_1_data_out2, m2_1_data_out2;

  not not_1 (not_1_out, Sel_Bus2[0]);
  not not_2 (not_2_out, Sel_Bus2[1]);
  nand nand_1 (nand_1_out, not_1_out, not_2_out);
  nor nor_1 (nor_1_out, nand_1_out, Sel_Bus2[2]);
  M1 m1_1 (
    .Data_In(Data_In), .Sel(Sel), .W_R(W_R1), .clk(clk), .reset(reset), .Data_Out(Data_Out),
    .Data_out2(m1_1_data_out2));
  M2 m2_1 (
    .Data_In(Data_In), .Sel(Sel), .W_R(W_R2), .clk(clk), .reset(reset), .Data_Out(Data_Out),
    .Data_out2(m2_1_data_out2));
  bus_con bus_con_1 (.enable(nor_1_out), .D(m1_1_data_out2), .Saida(RegM[7:0]));
  bus_con bus_con_2 (.enable(nor_1_out), .D(m2_1_data_out2), .Saida(RegM[15:8]));

  // Notes on the sheet:
  //   Data_In: pull=down
endmodule

module X (
  input  [7:0] Data_In,
  input  [3:0] Sel,
  input  W_R,
  input  clk,
  input  reset,
  output [7:0] Data_Out,
  output [7:0] Data_out2
);

  wire nand_1_out, nand_2_out, nor_1_out, not_1_out, not_2_out;

  not not_1 (not_1_out, Sel[0]);
  not not_2 (not_2_out, Sel[3]);
  nand nand_1 (nand_1_out, not_1_out, Sel[1]);
  nand nand_2 (nand_2_out, Sel[2], not_2_out);
  nor nor_1 (nor_1_out, nand_1_out, nand_2_out);
  RegBase regbase_1 (
    .enable(nor_1_out), .Data_In(Data_In), .W_R(W_R), .clk(clk), .reset(reset), .Data_Out(Data_Out),
    .Data_out_allways(Data_out2));

  // Notes on the sheet:
  //   Data_In: pull=down
endmodule

module Y (
  input  [7:0] Data_In,
  input  [3:0] Sel,
  input  W_R,
  input  clk,
  input  reset,
  output [7:0] Data_Out,
  output [7:0] Data_out2
);

  wire nand_1_out, nand_2_out, nor_1_out, not_1_out;

  not not_1 (not_1_out, Sel[3]);
  nand nand_1 (nand_1_out, Sel[0], Sel[1]);
  nand nand_2 (nand_2_out, Sel[2], not_1_out);
  nor nor_1 (nor_1_out, nand_1_out, nand_2_out);
  RegBase regbase_1 (
    .enable(nor_1_out), .Data_In(Data_In), .W_R(W_R), .clk(clk), .reset(reset), .Data_Out(Data_Out),
    .Data_out_allways(Data_out2));

  // Notes on the sheet:
  //   Data_In: pull=down
endmodule

module XY (
  input  [7:0] Data_In,
  input  [3:0] Sel,
  input  [2:0] Sel_Bus2,
  input  W_R1,
  input  bus_sel,
  input  W_R2,
  input  clk,
  input  reset,
  output [7:0] Data_Out,
  output [15:0] RegM
);

  wire nand_1_out, nor_1_out, not_1_out;
  wire [7:0] multiplexer_1_out, multiplexer_2_out, x_1_data_out2, y_1_data_out2;

  Multiplexer #(.width(8)) multiplexer_1 (.in0(Data_In), .in1(RegM[7:0]), .out(multiplexer_1_out), .sel(bus_sel));
  Multiplexer #(.width(8)) multiplexer_2 (.in0(Data_In), .in1(RegM[15:8]), .out(multiplexer_2_out), .sel(bus_sel));
  not not_1 (not_1_out, Sel_Bus2[1]);
  nand nand_1 (nand_1_out, Sel_Bus2[0], not_1_out);
  nor nor_1 (nor_1_out, nand_1_out, Sel_Bus2[2]);
  X x_1 (
    .Data_In(multiplexer_1_out), .Sel(Sel), .W_R(W_R1), .clk(clk), .reset(reset), .Data_Out(Data_In),
    .Data_out2(x_1_data_out2));
  Y y_1 (
    .Data_In(multiplexer_2_out), .Sel(Sel), .W_R(W_R2), .clk(clk), .reset(reset), .Data_Out(Data_In),
    .Data_out2(y_1_data_out2));
  bus_con bus_con_1 (.enable(nor_1_out), .D(x_1_data_out2), .Saida(RegM[7:0]));
  bus_con bus_con_2 (.enable(nor_1_out), .D(y_1_data_out2), .Saida(RegM[15:8]));

  assign Data_Out = Data_In;

  // Notes on the sheet:
  //   Data_In: pull=down
endmodule

module J1 (
  input  [7:0] Data_In,
  input  [3:0] Sel,
  input  W_R,
  input  clk,
  input  reset,
  output [7:0] Data_Out,
  output [7:0] Data_out2
);

  wire nand_1_out, nand_2_out, nor_1_out, not_1_out, not_2_out, not_3_out;

  not not_1 (not_1_out, Sel[0]);
  not not_2 (not_2_out, Sel[1]);
  not not_3 (not_3_out, Sel[2]);
  nand nand_1 (nand_1_out, not_1_out, not_2_out);
  nand nand_2 (nand_2_out, not_3_out, Sel[3]);
  nor nor_1 (nor_1_out, nand_1_out, nand_2_out);
  RegBase regbase_1 (
    .enable(nor_1_out), .Data_In(Data_In), .W_R(W_R), .clk(clk), .reset(reset), .Data_Out(Data_Out),
    .Data_out_allways(Data_out2));

  // Notes on the sheet:
  //   Data_In: pull=down
endmodule

module J2 (
  input  [7:0] Data_In,
  input  [3:0] Sel,
  input  W_R,
  input  clk,
  input  reset,
  output [7:0] Data_Out,
  output [7:0] Data_out2
);

  wire nand_1_out, nand_2_out, nor_1_out, not_1_out, not_2_out;

  not not_1 (not_1_out, Sel[1]);
  not not_2 (not_2_out, Sel[2]);
  nand nand_1 (nand_1_out, Sel[0], not_1_out);
  nand nand_2 (nand_2_out, not_2_out, Sel[3]);
  nor nor_1 (nor_1_out, nand_1_out, nand_2_out);
  RegBase regbase_1 (
    .enable(nor_1_out), .Data_In(Data_In), .W_R(W_R), .clk(clk), .reset(reset), .Data_Out(Data_Out),
    .Data_out_allways(Data_out2));

  // Notes on the sheet:
  //   Data_In: pull=down
endmodule

module J (
  input  [7:0] Data_In,
  input  [3:0] Sel,
  input  [2:0] Sel_Bus2,
  input  W_R1,
  input  W_R2,
  input  clk,
  input  reset,
  output [7:0] Data_Out,
  output [15:0] RegM
);

  wire nand_1_out, nor_1_out, not_1_out;
  wire [7:0] j1_1_data_out2, j2_1_data_out2;

  not not_1 (not_1_out, Sel_Bus2[0]);
  nand nand_1 (nand_1_out, not_1_out, Sel_Bus2[1]);
  nor nor_1 (nor_1_out, nand_1_out, Sel_Bus2[2]);
  J1 j1_1 (
    .Data_In(Data_In), .Sel(Sel), .W_R(W_R1), .clk(clk), .reset(reset), .Data_Out(Data_Out),
    .Data_out2(j1_1_data_out2));
  J2 j2_1 (
    .Data_In(Data_In), .Sel(Sel), .W_R(W_R2), .clk(clk), .reset(reset), .Data_Out(Data_Out),
    .Data_out2(j2_1_data_out2));
  bus_con bus_con_1 (.enable(nor_1_out), .D(j1_1_data_out2), .Saida(RegM[7:0]));
  bus_con bus_con_2 (.enable(nor_1_out), .D(j2_1_data_out2), .Saida(RegM[15:8]));

  // Notes on the sheet:
  //   Data_In: pull=down
endmodule

module Inst (
  input  [7:0] Data_In,
  input  W_R,
  input  clk,
  input  reset,
  output [7:0] const_out
);

  Register register_1 (.D(Data_In), .en(W_R), .clk(clk), .Q(const_out), .clr(reset));
endmodule

module PC (
  input  [2:0] Sel_Bus2,
  input  W_R1,
  input  clk,
  input  reset,
  input  [15:0] in_5,
  output [15:0] RegM
);

  wire nand_1_out, nor_1_out;
  wire [7:0] register_1_q, register_2_q;

  Register register_1 (.D(in_5[7:0]), .en(W_R1), .clk(clk), .Q(register_1_q), .clr(reset));
  Register register_2 (.D(in_5[15:8]), .en(W_R1), .clk(clk), .Q(register_2_q), .clr(reset));
  nand nand_1 (nand_1_out, Sel_Bus2[0], Sel_Bus2[1]);
  nor nor_1 (nor_1_out, nand_1_out, Sel_Bus2[2]);
  bus_con bus_con_1 (.enable(nor_1_out), .D(register_1_q), .Saida(RegM[7:0]));
  bus_con bus_con_2 (.enable(nor_1_out), .D(register_2_q), .Saida(RegM[15:8]));

  // Other names for the same wires on the sheet: r = reset
endmodule

module Inc (
  input  [2:0] Sel_Bus2,
  input  W_R1,
  input  clk,
  input  reset,
  input  [15:0] in_5,
  output [15:0] RegM
);

  wire nand_1_out, nor_1_out, not_1_out, not_2_out, not_3_out;
  wire [7:0] register_1_q, register_2_q;

  Register register_1 (.D(in_5[7:0]), .en(W_R1), .clk(clk), .Q(register_1_q), .clr(reset));
  Register register_2 (.D(in_5[15:8]), .en(W_R1), .clk(clk), .Q(register_2_q), .clr(reset));
  not not_1 (not_1_out, Sel_Bus2[0]);
  not not_2 (not_2_out, Sel_Bus2[1]);
  nand nand_1 (nand_1_out, not_1_out, not_2_out);
  nor nor_1 (nor_1_out, nand_1_out, not_3_out);
  not not_3 (not_3_out, Sel_Bus2[2]);
  bus_con bus_con_1 (.enable(nor_1_out), .D(register_1_q), .Saida(RegM[7:0]));
  bus_con bus_con_2 (.enable(nor_1_out), .D(register_2_q), .Saida(RegM[15:8]));

  // Other names for the same wires on the sheet: r = reset
endmodule

module RegBase (
  input  enable,
  input  [7:0] Data_In,
  input  W_R,
  input  clk,
  input  reset,
  output [7:0] Data_Out,
  output [7:0] Data_out_allways
);

  Register Registrador (.D(Data_In), .en(W_R), .clk(clk), .Q(Data_out_allways), .clr(reset));
  bus_con bus_con_1 (.enable(enable), .D(Data_out_allways), .Saida(Data_Out));
endmodule

module Bus_con_1bit (
  input  Enable,
  input  D,
  output Saida
);

  wire transistor_2_out;

  Transistor #(.\type ("n")) transistor_1 (.in(transistor_2_out), .out(Saida), .gate(Enable));
  Transistor #(.\type ("n")) transistor_2 (.in(1'b0), .out(transistor_2_out), .gate(D));
endmodule

module bus_pull_up (
  input  [7:0] in_1,
  output [7:0] out_2
);

  Pull_Resistor #(.pull(1)) pull_resistor_1 (.node(in_1[0]));
  Pull_Resistor #(.pull(1)) pull_resistor_2 (.node(in_1[1]));
  Pull_Resistor #(.pull(1)) pull_resistor_3 (.node(in_1[2]));
  Pull_Resistor #(.pull(1)) pull_resistor_4 (.node(in_1[3]));
  Pull_Resistor #(.pull(1)) pull_resistor_5 (.node(in_1[4]));
  Pull_Resistor #(.pull(1)) pull_resistor_6 (.node(in_1[5]));
  Pull_Resistor #(.pull(1)) pull_resistor_7 (.node(in_1[6]));
  Pull_Resistor #(.pull(1)) pull_resistor_8 (.node(in_1[7]));

  assign out_2 = in_1;
endmodule

// B_Con
module bus_con (
  input  enable,
  input  [7:0] D,
  output [7:0] Saida
);

  wire [7:0] not_1_out;

  assign not_1_out = ~D;  // NOT_Gate not_1, 8 bits wide
  Bus_con_1bit bus_con_1bit_1 (.Enable(enable), .D(not_1_out[0]), .Saida(Saida[0]));
  Bus_con_1bit bus_con_1bit_2 (.Enable(enable), .D(not_1_out[1]), .Saida(Saida[1]));
  Bus_con_1bit bus_con_1bit_3 (.Enable(enable), .D(not_1_out[2]), .Saida(Saida[2]));
  Bus_con_1bit bus_con_1bit_4 (.Enable(enable), .D(not_1_out[3]), .Saida(Saida[3]));
  Bus_con_1bit bus_con_1bit_5 (.Enable(enable), .D(not_1_out[4]), .Saida(Saida[4]));
  Bus_con_1bit bus_con_1bit_6 (.Enable(enable), .D(not_1_out[5]), .Saida(Saida[5]));
  Bus_con_1bit bus_con_1bit_7 (.Enable(enable), .D(not_1_out[6]), .Saida(Saida[6]));
  Bus_con_1bit bus_con_1bit_8 (.Enable(enable), .D(not_1_out[7]), .Saida(Saida[7]));
endmodule

module bus_con_16 (
  input  Enable,
  input  [15:0] Entrada,
  output [15:0] Saida
);

  bus_con bus_con_1 (.enable(Enable), .D(Entrada[7:0]), .Saida(Saida[7:0]));
  bus_con bus_con_2 (.enable(Enable), .D(Entrada[15:8]), .Saida(Saida[15:8]));
endmodule
