// Logisim project t.circ as structural Verilog: 2 circuits, main circuit main
module main (
  input  [1:0] in_1,
  input  [1:0] in_2,
  output [1:0] out_3
);
endmodule

module sop (
  input  [1:0] A,
  input  [1:0] B,
  output [1:0] S
);

  wire A0_n, A1_n, and_2_out, and_4_out, and_6_out, and_8_out, and_9_out, and_11_out, and_12_out, and_14_out,
       B0_n, B1_n, L_t0_241175a4, L_t1_7bf54020, L_t2_80a45623, L_t3_d1372e32, L_t4_7557f385, L_t5_f1a577f9,
       L_t6_2eedd94f, L_t7_df0a5c32, or_1_out, or_2_out, or_3_out, or_4_out;

  not not_1 (A1_n, A[1]);
  not not_2 (A0_n, A[0]);
  not not_3 (B1_n, B[0]);
  not not_4 (B0_n, B[1]);
  and and_1 (L_t0_241175a4, A[1], and_2_out);
  and and_2 (and_2_out, A0_n, B1_n);
  and and_3 (L_t1_7bf54020, A1_n, and_4_out);
  and and_4 (and_4_out, A0_n, B[0]);
  and and_5 (L_t2_80a45623, A[1], and_6_out);
  and and_6 (and_6_out, B1_n, B0_n);
  and and_7 (L_t3_d1372e32, A1_n, and_8_out);
  and and_8 (and_8_out, B[0], B0_n);
  and and_9 (and_9_out, A1_n, A[0]);
  and and_10 (L_t4_7557f385, and_9_out, and_11_out);
  and and_11 (and_11_out, B1_n, B[1]);
  and and_12 (and_12_out, A[1], A[0]);
  and and_13 (L_t5_f1a577f9, and_12_out, and_14_out);
  and and_14 (and_14_out, B[0], B[1]);
  and and_15 (L_t6_2eedd94f, A[0], B0_n);
  and and_16 (L_t7_df0a5c32, A0_n, B[1]);
  or or_1 (or_1_out, L_t1_7bf54020, L_t2_80a45623);
  or or_2 (or_2_out, L_t4_7557f385, L_t5_f1a577f9);
  or or_3 (or_3_out, L_t0_241175a4, or_1_out);
  or or_4 (or_4_out, L_t3_d1372e32, or_2_out);
  or or_5 (S[1], or_3_out, or_4_out);
  or or_6 (S[0], L_t6_2eedd94f, L_t7_df0a5c32);

  // Other names for the same wires on the sheet: B1 = B[0]; B0 = B[1]; L_go_S0_936e1ade = S[0];
  //   L_go_S1_24fb4840 = S[1]
endmodule
