// Logisim project temp.circ as structural Verilog: 1 circuit, main circuit sop
module sop (
  input  in0,
  input  in1,
  input  in2,
  input  in3,
  input  in4,
  input  in5,
  output out0,
  output out1,
  output out2,
  output out3,
  output out4,
  output out5,
  output out6,
  output out7
);

  wire _t0, _t1, _t2, _t3, _t4, _t5, _t6, _t7, _t8, _t9, _t10, _t11, _t12, _t13, _t14, _t15, _t16, _t17,
       _t18, _t19, _t20, _t21, _t22, _t23, _t24, _t25, _t26, _t27, _t28, _t29, and_1_out, and_2_out,
       and_3_out, and_4_out, and_6_out, and_7_out, and_9_out, and_11_out, and_12_out, and_14_out, and_15_out,
       and_17_out, and_18_out, and_20_out, and_22_out, and_23_out, and_25_out, and_27_out, and_28_out,
       and_30_out, and_32_out, and_33_out, and_35_out, and_37_out, and_38_out, and_40_out, and_41_out,
       and_43_out, and_46_out, and_48_out, and_49_out, and_51_out, and_53_out, and_55_out, and_56_out,
       and_58_out, and_59_out, and_61_out, and_62_out, and_64_out, and_65_out, and_67_out, and_68_out,
       and_70_out, and_72_out, and_74_out, and_75_out, and_77_out, and_78_out, and_80_out, in0_n, in1_n,
       in2_n, in3_n, in4_n, in5_n, or_1_out, or_2_out, or_3_out, or_4_out, or_5_out, or_6_out, or_7_out,
       or_8_out, or_9_out, or_10_out, or_11_out, or_12_out, or_13_out, or_14_out;

  not not_1 (in0_n, in0);
  not not_2 (in1_n, in1);
  not not_3 (in2_n, in2);
  not not_4 (in3_n, in3);
  not not_5 (in4_n, in4);
  not not_6 (in5_n, in5);
  and and_1 (and_1_out, in3_n, in4);
  and and_2 (and_2_out, in3_n, in4);
  and and_3 (and_3_out, in3_n, in4);
  and and_4 (and_4_out, in0_n, in1);
  and and_5 (_t0, and_4_out, and_6_out);
  and and_6 (and_6_out, in2_n, in3);
  and and_7 (and_7_out, in0_n, in1_n);
  and and_8 (_t1, and_7_out, and_9_out);
  and and_9 (and_9_out, in3, in4);
  and and_10 (_t2, in0_n, and_11_out);
  and and_11 (and_11_out, in2_n, in4);
  and and_12 (and_12_out, in0_n, in1_n);
  and and_13 (_t3, and_12_out, and_14_out);
  and and_14 (and_14_out, in2, and_1_out);
  and and_15 (and_15_out, in0_n, in1_n);
  and and_16 (_t4, and_15_out, and_17_out);
  and and_17 (and_17_out, in3, in4);
  and and_18 (and_18_out, in0_n, in1_n);
  and and_19 (_t5, and_18_out, and_20_out);
  and and_20 (and_20_out, in2_n, in3);
  and and_21 (_t6, in0_n, and_22_out);
  and and_22 (and_22_out, in2_n, in4);
  and and_23 (and_23_out, in0_n, in1_n);
  and and_24 (_t7, and_23_out, and_25_out);
  and and_25 (and_25_out, in2, in3);
  and and_26 (_t8, in0_n, and_27_out);
  and and_27 (and_27_out, in1, in2_n);
  and and_28 (and_28_out, in0_n, in1_n);
  and and_29 (_t9, and_28_out, and_30_out);
  and and_30 (and_30_out, in2_n, in3_n);
  and and_31 (_t10, in0_n, and_32_out);
  and and_32 (and_32_out, in1, in2_n);
  and and_33 (and_33_out, in0_n, in1_n);
  and and_34 (_t11, and_33_out, and_35_out);
  and and_35 (and_35_out, in2_n, in3);
  and and_36 (_t12, in1, and_37_out);
  and and_37 (and_37_out, in2, in3_n);
  and and_38 (and_38_out, in0_n, in1);
  and and_39 (_t13, and_38_out, and_40_out);
  and and_40 (and_40_out, in2, in4_n);
  and and_41 (and_41_out, in0_n, in1_n);
  and and_42 (_t14, and_41_out, and_43_out);
  and and_43 (and_43_out, in2_n, in3_n);
  and and_44 (_t15, in0, in5_n);
  and and_45 (_t16, in0, in5);
  and and_46 (and_46_out, in0_n, in1);
  and and_47 (_t17, and_46_out, and_48_out);
  and and_48 (and_48_out, in3, in4);
  and and_49 (and_49_out, in0_n, in1);
  and and_50 (_t18, and_49_out, and_51_out);
  and and_51 (and_51_out, in2, in4_n);
  and and_52 (_t19, in0, in5_n);
  and and_53 (and_53_out, in0_n, in1_n);
  and and_54 (_t20, and_53_out, and_55_out);
  and and_55 (and_55_out, in2_n, in3);
  and and_56 (and_56_out, in0_n, in1_n);
  and and_57 (_t21, and_56_out, and_58_out);
  and and_58 (and_58_out, in2, and_2_out);
  and and_59 (and_59_out, in0_n, in2);
  and and_60 (_t22, and_59_out, and_61_out);
  and and_61 (and_61_out, in3_n, in4_n);
  and and_62 (and_62_out, in0_n, in1);
  and and_63 (_t23, and_62_out, and_64_out);
  and and_64 (and_64_out, in3, in4);
  and and_65 (and_65_out, in0_n, in1);
  and and_66 (_t24, and_65_out, and_67_out);
  and and_67 (and_67_out, in2, in4_n);
  and and_68 (and_68_out, in0_n, in1_n);
  and and_69 (_t25, and_68_out, and_70_out);
  and and_70 (and_70_out, in2_n, in3_n);
  and and_71 (_t26, in0, in5);
  and and_72 (and_72_out, in0_n, in1_n);
  and and_73 (_t27, and_72_out, and_74_out);
  and and_74 (and_74_out, in2, and_3_out);
  and and_75 (and_75_out, in0_n, in2);
  and and_76 (_t28, and_75_out, and_77_out);
  and and_77 (and_77_out, in3_n, in4_n);
  and and_78 (and_78_out, in0_n, in1_n);
  and and_79 (_t29, and_78_out, and_80_out);
  and and_80 (and_80_out, in2_n, in3);
  or or_1 (or_1_out, _t15, _t16);
  or or_2 (or_2_out, _t22, _t23);
  or or_3 (or_3_out, _t25, _t26);
  or or_4 (or_4_out, _t1, _t2);
  or or_5 (or_5_out, _t3, _t4);
  or or_6 (or_6_out, _t5, _t6);
  or or_7 (or_7_out, _t10, _t11);
  or or_8 (or_8_out, _t12, _t13);
  or or_9 (or_9_out, _t14, or_1_out);
  or or_10 (or_10_out, _t17, _t18);
  or or_11 (or_11_out, _t19, _t20);
  or or_12 (or_12_out, _t21, or_2_out);
  or or_13 (or_13_out, _t24, or_3_out);
  or or_14 (or_14_out, _t28, _t29);
  or or_15 (out0, _t0, or_4_out);
  or or_16 (out1, or_5_out, or_6_out);
  or or_17 (out2, _t7, _t8);
  or or_18 (out3, _t9, or_7_out);
  or or_19 (out4, or_8_out, or_9_out);
  or or_20 (out5, or_10_out, or_11_out);
  or or_21 (out6, or_12_out, or_13_out);
  or or_22 (out7, _t27, or_14_out);
endmodule
