// Logisim project teste.circ as structural Verilog: 1 circuit, main circuit main
module main (
  input  [2:0] in_1,
  input  [1:0] in_2,
  output [2:0] out_3,
  output [4:0] out_4
);

  // PlaRom #(.Contents("2 1 0 0 1 2 0 1 1 0 1 2 2 0 2 1 0 2*4 1 1 0*3 1 2 1 2 2 1 0 1 2 0 2*4 0 2 0 1 1 0 2 1 1 0 2 0 0 1*3 2 0 2 0 0 1 0 2 1 0 1 1 2 0*3 2 0 1 0 0 1 0 2 1 0 0 1 0 0 1 0 0 1 0 0 1 0*3 1 0 1 0*3 1 0 0 1 0 0 1 0 1 0 0 1 0*3 1 0 0 1 0*3 1 0 0 1"), .\and (16), .outputs(3)) rom: pin names not known; wires that end beside it: {in_1, in_2}, out_3

  assign out_4 = {in_1, in_2};
endmodule
